// Logisim project LogisimDesign.circ as structural Verilog: 45 circuits, main circuit flip_flop
module main (
  output [17:0] out_1
);

  wire alu_1_reg1_is_zero, and_1_out, and_2_out, buffer_1_out, buffer_2_out, buffer_3_out, buffer_4_out,
       buffer_5_out, buffer_6_out, buffer_7_out, buffer_8_out, buffer_9_out, buffer_10_out, buffer_11_out,
       buffer_12_out, buffer_13_out, buffer_14_out, buffer_15_out, buffer_16_out, buffer_17_out,
       buffer_18_out, buffer_19_out, buffer_20_out, buffer_21_out, buffer_22_out, clock_1_out,
       control_unit_1_alu_input_control, control_unit_1_cmov, control_unit_1_decrement_stack_ptr,
       control_unit_1_increment_stack_ptr, control_unit_1_jal, control_unit_1_ld, control_unit_1_lui,
       control_unit_1_pc_clock_signal, control_unit_1_pc_write, control_unit_1_read_stack, control_unit_1_st,
       control_unit_1_stack_op_state1, control_unit_1_we, control_unit_1_write_to_stack, flip_flop_1_out,
       flip_flop_2_out, multiplexer_3_out, multiplexer_4_out, not_1_out, not_2_out, not_3_out, not_4_out,
       not_5_out, not_6_out, not_7_out, not_8_out, not_9_out, not_10_out, or_1_out, or_2_out, or_3_out,
       or_4_out, or_5_out, reset_start_out;
  wire [3:0] control_unit_1_address_of_dest, control_unit_1_address_of_src1, control_unit_1_address_of_src2,
       control_unit_1_alu_control_signal, controlled_buffer_2_out, controlled_buffer_4_out;
  wire [5:0] control_unit_1__6_bits_imm;
  wire [9:0] control_unit_1__10_bits_imm;
  wire [11:0] adder_12_bits_1_output, controlled_buffer_1_out, multiplexer_1_out, multiplexer_2_out,
       n13_to_12_converter_1_out_2, n18b_to_12b_converter_1_output, pc_1_output, pc_1_output_1,
       zero_extent_10to12_1_out_2;
  wire [12:0] alu_1__13bout, control_unit_1__13_bits_imm, n12_to_13_zero_ext_1_out_2;
  wire [17:0] alu_1_stdout, controlled_buffer_6_out, controlled_buffer_10_out, controlled_buffer_11_out,
       controlled_buffer_12_out, controlled_buffer_14_out, controlled_buffer_16_out,
       controlled_buffer_18_out, controlled_buffer_19_out, converter_10_9_18_upper_1_out, ram_1_data,
       register_file_1_rd1, register_file_1_rd2, register_file_1_stack_pointer_register, rom_1_data,
       zero_ext_6_bits_1_out_2, zero_ext_12_bits_1_out_2, zero_ext_12_bits_2_out_2;

  assign controlled_buffer_1_out = control_unit_1_pc_write ? n13_to_12_converter_1_out_2 : 12'bz;  // Controlled_Buffer controlled_buffer_1
  Clock clock_1 (.out(clock_1_out));
  PC pc_1 (
    .clock(and_1_out), .\input (controlled_buffer_1_out), .\output (pc_1_output),
    .we(control_unit_1_pc_write), .reset(or_3_out), .output_1(pc_1_output_1));
  buf buffer_1 (buffer_1_out, buffer_2_out);
  buf buffer_2 (buffer_2_out, buffer_9_out);
  and and_1 (and_1_out, buffer_1_out, control_unit_1_pc_clock_signal);
  buf buffer_3 (buffer_3_out, buffer_4_out);
  buf buffer_4 (buffer_4_out, buffer_12_out);
  buf buffer_5 (buffer_5_out, buffer_6_out);
  buf buffer_6 (buffer_6_out, buffer_14_out);
  buf buffer_7 (buffer_7_out, buffer_8_out);
  buf buffer_8 (buffer_8_out, buffer_15_out);
  or or_1 (or_1_out, clock_1_out, reset_start_out);
  buf buffer_9 (buffer_9_out, buffer_10_out);
  buf buffer_10 (buffer_10_out, buffer_3_out);
  buf buffer_11 (buffer_11_out, buffer_5_out);
  buf buffer_12 (buffer_12_out, buffer_11_out);
  buf buffer_13 (buffer_13_out, buffer_7_out);
  buf buffer_14 (buffer_14_out, buffer_13_out);
  buf buffer_15 (buffer_15_out, buffer_16_out);
  buf buffer_16 (buffer_16_out, buffer_22_out);
  zero_ext_12_bits zero_ext_12_bits_1 (.in_1(pc_1_output_1), .out_2(zero_ext_12_bits_1_out_2));
  buf buffer_17 (buffer_17_out, buffer_18_out);
  buf buffer_18 (buffer_18_out, buffer_19_out);
  buf buffer_19 (buffer_19_out, or_1_out);
  Button reset_start (.out(reset_start_out));
  ROM #(.addrWidth(12), .dataWidth(18)) rom_1 (.addr(pc_1_output), .data(rom_1_data), .sel(1'b1));
  or or_2 (or_2_out, reset_start_out, flip_flop_2_out);
  buf buffer_20 (buffer_20_out, buffer_21_out);
  buf buffer_21 (buffer_21_out, buffer_17_out);
  buf buffer_22 (buffer_22_out, buffer_20_out);
  or or_3 (or_3_out, reset_start_out, flip_flop_1_out, flip_flop_2_out);
  flip_flop flip_flop_1 (.in(flip_flop_2_out), .clock(buffer_22_out), .out(flip_flop_1_out));
  flip_flop flip_flop_2 (.in(reset_start_out), .clock(buffer_22_out), .out(flip_flop_2_out));
  CONTROL_UNIT control_unit_1 (
    .instruction(rom_1_data), .ALU_input_control(control_unit_1_alu_input_control),
    .ALU_control_signal(control_unit_1_alu_control_signal), .we(control_unit_1_we),
    .address_of_src1(control_unit_1_address_of_src1), .address_of_src2(control_unit_1_address_of_src2),
    ._6_bits_imm(control_unit_1__6_bits_imm), ._13_bits_imm(control_unit_1__13_bits_imm),
    .pc_write(control_unit_1_pc_write), .jal(control_unit_1_jal), .ld(control_unit_1_ld),
    .st(control_unit_1_st), .lui(control_unit_1_lui), .cmov(control_unit_1_cmov),
    .read_stack(control_unit_1_read_stack), .decrement_stack_ptr(control_unit_1_decrement_stack_ptr),
    .increment_stack_ptr(control_unit_1_increment_stack_ptr), .write_to_stack(control_unit_1_write_to_stack),
    .reset(or_2_out), .clock(buffer_22_out), ._10_bits_imm(control_unit_1__10_bits_imm),
    .pc_clock_signal(control_unit_1_pc_clock_signal), .address_of_dest(control_unit_1_address_of_dest),
    .cmov_condition(alu_1_reg1_is_zero), .stack_op_state1(control_unit_1_stack_op_state1));
  or or_4 (or_4_out, control_unit_1_increment_stack_ptr, control_unit_1_decrement_stack_ptr);
  _12_to_13_zero_ext u_12_to_13_zero_ext_1 (.in_1(pc_1_output), .out_2(n12_to_13_zero_ext_1_out_2));
  not not_1 (not_1_out, control_unit_1_jal);
  assign controlled_buffer_2_out = not_1_out ? control_unit_1_address_of_dest : 4'bz;  // Controlled_Buffer controlled_buffer_2
  assign controlled_buffer_2_out = control_unit_1_jal ? 4'b1111 : 4'bz;  // Controlled_Buffer controlled_buffer_3
  not not_2 (not_2_out, or_4_out);
  assign controlled_buffer_4_out = not_2_out ? controlled_buffer_2_out : 4'bz;  // Controlled_Buffer controlled_buffer_4
  assign controlled_buffer_4_out = or_4_out ? 4'b1110 : 4'bz;  // Controlled_Buffer controlled_buffer_5
  or or_5 (or_5_out, control_unit_1_read_stack, control_unit_1_decrement_stack_ptr, control_unit_1_stack_op_state1, control_unit_1_increment_stack_ptr, control_unit_1_write_to_stack);
  zero_ext_6_bits zero_ext_6_bits_1 (.in_1(control_unit_1__6_bits_imm), .out_2(zero_ext_6_bits_1_out_2));
  not not_3 (not_3_out, or_4_out);
  assign controlled_buffer_6_out = not_3_out ? controlled_buffer_12_out : 18'bz;  // Controlled_Buffer controlled_buffer_6
  assign controlled_buffer_6_out = or_4_out ? zero_ext_12_bits_2_out_2 : 18'bz;  // Controlled_Buffer controlled_buffer_7
  not not_4 (not_4_out, control_unit_1_read_stack);
  assign out_1 = not_4_out ? controlled_buffer_6_out : 18'bz;  // Controlled_Buffer controlled_buffer_8
  assign out_1 = control_unit_1_read_stack ? ram_1_data : 18'bz;  // Controlled_Buffer controlled_buffer_9
  assign controlled_buffer_10_out = not_6_out ? register_file_1_rd1 : 18'bz;  // Controlled_Buffer controlled_buffer_10
  assign controlled_buffer_11_out = not_6_out ? controlled_buffer_14_out : 18'bz;  // Controlled_Buffer controlled_buffer_11
  assign controlled_buffer_12_out = not_7_out ? controlled_buffer_16_out : 18'bz;  // Controlled_Buffer controlled_buffer_12
  assign controlled_buffer_12_out = control_unit_1_cmov ? register_file_1_rd2 : 18'bz;  // Controlled_Buffer controlled_buffer_13
  assign controlled_buffer_14_out = control_unit_1_alu_input_control ? zero_ext_6_bits_1_out_2 : 18'bz;  // Controlled_Buffer controlled_buffer_14
  assign controlled_buffer_14_out = not_5_out ? register_file_1_rd2 : 18'bz;  // Controlled_Buffer controlled_buffer_15
  not not_5 (not_5_out, control_unit_1_alu_input_control);
  and and_2 (and_2_out, ~control_unit_1_alu_control_signal[3], control_unit_1_alu_control_signal[2], control_unit_1_alu_control_signal[1], control_unit_1_alu_control_signal[0]);  // AND_Gate
  not not_6 (not_6_out, and_2_out);
  converter_10__9__18_upper converter_10_9_18_upper_1 (
    .in(control_unit_1__10_bits_imm), .out(converter_10_9_18_upper_1_out));
  ALU alu_1 (
    .control_signal(control_unit_1_alu_control_signal), .input_1(controlled_buffer_10_out),
    .input_2(controlled_buffer_11_out), .stdout(alu_1_stdout), .i13_1(control_unit_1__13_bits_imm),
    .i13_2(n12_to_13_zero_ext_1_out_2), ._13bout(alu_1__13bout), .reg1_is_zero(alu_1_reg1_is_zero));
  assign controlled_buffer_16_out = not_8_out ? controlled_buffer_19_out : 18'bz;  // Controlled_Buffer controlled_buffer_16
  not not_7 (not_7_out, control_unit_1_cmov);
  not not_8 (not_8_out, control_unit_1_jal);
  assign controlled_buffer_16_out = control_unit_1_jal ? zero_ext_12_bits_1_out_2 : 18'bz;  // Controlled_Buffer controlled_buffer_17
  zero_ext_12_bits zero_ext_12_bits_2 (.in_1(adder_12_bits_1_output), .out_2(zero_ext_12_bits_2_out_2));
  REGISTER_FILE register_file_1 (
    .clock(buffer_22_out), .\input (out_1), .wr(controlled_buffer_4_out), .rd1(register_file_1_rd1),
    .ra1(control_unit_1_address_of_src1), .rd2(register_file_1_rd2), .ra2(control_unit_1_address_of_src2),
    .we(control_unit_1_we), .reset(reset_start_out),
    .stack_pointer_register(register_file_1_stack_pointer_register));
  zero_extent_10to12 zero_extent_10to12_1 (.in_1(control_unit_1__10_bits_imm), .out_2(zero_extent_10to12_1_out_2));
  not not_9 (not_9_out, control_unit_1_ld);
  assign controlled_buffer_18_out = not_9_out ? alu_1_stdout : 18'bz;  // Controlled_Buffer controlled_buffer_18
  assign controlled_buffer_19_out = not_10_out ? controlled_buffer_18_out : 18'bz;  // Controlled_Buffer controlled_buffer_19
  not not_10 (not_10_out, control_unit_1_lui);
  assign controlled_buffer_19_out = control_unit_1_lui ? converter_10_9_18_upper_1_out : 18'bz;  // Controlled_Buffer controlled_buffer_20
  Multiplexer #(.width(12), .enable("false")) multiplexer_1 (
    .in0({12{1'b1}}), .in1(12'h1), .out(multiplexer_1_out), .sel(control_unit_1_decrement_stack_ptr));
  adder_12_bits adder_12_bits_1 (
    .input_1(n18b_to_12b_converter_1_output), .\output (adder_12_bits_1_output), .input_2(multiplexer_1_out));  // open: c_out
  Multiplexer #(.width(12), .enable("false")) multiplexer_2 (
    .in0(zero_extent_10to12_1_out_2), .in1(n18b_to_12b_converter_1_output), .out(multiplexer_2_out),
    .sel(or_5_out));
  _13_to_12_converter u_13_to_12_converter_1 (.in_1(alu_1__13bout), .out_2(n13_to_12_converter_1_out_2));
  _18b_to_12b_converter u_18b_to_12b_converter_1 (
    .\input (register_file_1_stack_pointer_register), .\output (n18b_to_12b_converter_1_output));
  Multiplexer #(.enable("false")) multiplexer_3 (
    .in0(control_unit_1_st), .in1(control_unit_1_write_to_stack), .out(multiplexer_3_out), .sel(or_5_out));
  assign controlled_buffer_18_out = control_unit_1_ld ? ram_1_data : 18'bz;  // Controlled_Buffer controlled_buffer_21
  RAM #(.addrWidth(12), .dataWidth(18), .bus("separate")) ram_1 (
    .addr(multiplexer_2_out), .din(register_file_1_rd1), .data(ram_1_data), .str(multiplexer_3_out),
    .clk(buffer_22_out), .ld(multiplexer_4_out));  // open: sel, clr
  Multiplexer #(.enable("false")) multiplexer_4 (
    .in0(control_unit_1_ld), .in1(control_unit_1_read_stack), .out(multiplexer_4_out), .sel(or_5_out));

  // Notes on the sheet:
  //   contents of rom_1 (hex, n*v repeats v):
  //   1c000 1c401 1c803 cc01 25809 38033 4cd2 38033 38024 21005 20806 4964 a004 cc01 cc01 8002 9fff 9ffe
  //   DATA_MEMORY
endmodule

module ALU (
  input  [3:0] control_signal,
  input  [17:0] input_1,
  input  [17:0] input_2,
  input  [12:0] i13_1,
  input  [12:0] i13_2,
  output [17:0] stdout,
  output [12:0] _13bout,
  output reg1_is_zero
);

  wire [17:0] adder_18_bits_1_output, adder_18_bits_2_output, adder_18_bits_3_output, nand_1_out, nor_1_out,
       not_1_out, right_shifter_master_1_out_4, right_shifter_master_2_out_4;

  adder_18_bits adder_18_bits_1 (
    .input_1(not_1_out), .\output (adder_18_bits_1_output), .input_2(18'h1));  // open: c_out
  assign not_1_out = ~input_2;  // NOT_Gate not_1, 18 bits wide
  adder_13_bits adder_13_bits_1 (.input_1(i13_1), .\output (_13bout), .input_2(i13_2));  // open: c_out
  adder_18_bits adder_18_bits_2 (
    .input_1(input_1), .\output (adder_18_bits_2_output), .input_2(input_2));  // open: c_out
  adder_18_bits adder_18_bits_3 (
    .input_1(input_1), .\output (adder_18_bits_3_output), .input_2(adder_18_bits_1_output));  // open: c_out
  assign nand_1_out = ~(input_1 & input_2);  // NAND_Gate nand_1, 18 bits wide
  assign nor_1_out = ~(input_1 | input_2);  // NOR_Gate nor_1, 18 bits wide
  right_shifter_master right_shifter_master_1 (
    .l_a(1'b0), .input_1(input_1), .input_2(input_2), .out_4(right_shifter_master_1_out_4));
  right_shifter_master right_shifter_master_2 (
    .l_a(1'b1), .input_1(input_1), .input_2(input_2), .out_4(right_shifter_master_2_out_4));
  Multiplexer #(.select(3), .width(18), .enable("false")) multiplexer_1 (
    .in1(adder_18_bits_2_output), .in2(adder_18_bits_3_output), .in3(nand_1_out), .in4(nor_1_out),
    .in5(right_shifter_master_1_out_4), .in6(right_shifter_master_2_out_4), .out(stdout),
    .sel(control_signal[2:0]));  // open: in0, in7
  and and_1 (reg1_is_zero, ~input_1[0], ~input_1[1], ~input_1[2], ~input_1[3], ~input_1[4], ~input_1[5], ~input_1[6], ~input_1[7], ~input_1[8], ~input_1[10], ~input_1[11], ~input_1[12], ~input_1[13], ~input_1[14], ~input_1[15], ~input_1[16], ~input_1[17], ~input_1[9]);  // AND_Gate
endmodule

module CONTROL_UNIT (
  input  [17:0] instruction,
  input  reset,
  input  clock,
  input  cmov_condition,
  output [12:0] _13_bits_imm,
  output [5:0] _6_bits_imm,
  output [9:0] _10_bits_imm,
  output [3:0] ALU_control_signal,
  output ALU_input_control,
  output st,
  output we,
  output pc_write,
  output jal,
  output [3:0] address_of_dest,
  output ld,
  output [3:0] address_of_src2,
  output [3:0] address_of_src1,
  output stack_op_state1,
  output lui,
  output cmov,
  output read_stack,
  output decrement_stack_ptr,
  output increment_stack_ptr,
  output write_to_stack,
  output pc_clock_signal
);

  wire and_1_out, and_2_out, and_3_out, and_4_out, and_5_out, and_6_out, and_7_out, and_8_out, and_9_out,
       and_10_out, and_11_out, and_12_out, and_13_out, and_14_out, and_15_out, and_16_out, and_17_out,
       and_18_out, and_19_out, and_20_out, and_21_out, and_22_out, and_23_out, and_24_out, and_25_out,
       and_27_out, and_33_out, and_34_out, and_35_out, and_36_out, and_37_out, and_41_out, buffer_1_out,
       buffer_2_out, buffer_3_out, buffer_4_out, decoder_1_out2, decoder_1_out4, decoder_1_out5,
       decoder_1_out6, decoder_1_out7, decoder_1_out8, decoder_1_out10, decoder_1_out14, decoder_1_out15,
       flip_flop_1_out, flip_flop_2_out, flip_flop_3_out, not_1_out, not_2_out, not_3_out, not_4_out,
       not_5_out, not_6_out, or_1_out, or_3_out, or_6_out, or_7_out, or_8_out, or_9_out, or_10_out,
       or_11_out, or_13_out;
  wire [3:0] and_29_out, and_30_out, controlled_buffer_1_out, controlled_buffer_2_out,
       controlled_buffer_3_out, controlled_buffer_7_out, controlled_buffer_9_out, multiplexer_1_out,
       multiplexer_2_out, multiplexer_3_out, multiplexer_4_out, register_4_bits_1_out1;
  wire [3:3] and_26_out;

  assign controlled_buffer_1_out = reset ? 4'b0000 : 4'bz;  // Controlled_Buffer controlled_buffer_1
  assign controlled_buffer_2_out = reset ? 4'b0000 : 4'bz;  // Controlled_Buffer controlled_buffer_2
  not not_1 (not_1_out, reset);
  assign controlled_buffer_3_out = reset ? 4'b0000 : 4'bz;  // Controlled_Buffer controlled_buffer_3
  assign controlled_buffer_3_out = not_1_out ? controlled_buffer_9_out : 4'bz;  // Controlled_Buffer controlled_buffer_4
  register_4_bits register_4_bits_1 (
    .clock(clock), .in4(controlled_buffer_3_out[3]), .in3(controlled_buffer_3_out[2]),
    .in2(controlled_buffer_3_out[1]), .in1(controlled_buffer_3_out[0]), .out4(register_4_bits_1_out1[3]),
    .out3(register_4_bits_1_out1[2]), .out2(register_4_bits_1_out1[1]), .out1(register_4_bits_1_out1[0]));
  assign controlled_buffer_2_out = not_2_out ? register_4_bits_1_out1 : 4'bz;  // Controlled_Buffer controlled_buffer_5
  not not_2 (not_2_out, reset);
  assign controlled_buffer_1_out = not_3_out ? instruction[13:10] : 4'bz;  // Controlled_Buffer controlled_buffer_6
  not not_3 (not_3_out, reset);
  and and_1 (and_1_out, register_4_bits_1_out1[0], register_4_bits_1_out1[1], ~register_4_bits_1_out1[2], ~register_4_bits_1_out1[3]);  // AND_Gate
  and and_2 (and_2_out, ~register_4_bits_1_out1[0], ~register_4_bits_1_out1[1], ~register_4_bits_1_out1[2], ~register_4_bits_1_out1[3]);  // AND_Gate
  and and_3 (and_3_out, ~register_4_bits_1_out1[0], register_4_bits_1_out1[1], ~register_4_bits_1_out1[2], ~register_4_bits_1_out1[3]);  // AND_Gate
  and and_4 (and_4_out, register_4_bits_1_out1[0], ~register_4_bits_1_out1[1], register_4_bits_1_out1[2], ~register_4_bits_1_out1[3], ~instruction[17]);  // AND_Gate
  and and_5 (and_5_out, register_4_bits_1_out1[0], register_4_bits_1_out1[1], register_4_bits_1_out1[2], ~register_4_bits_1_out1[3]);  // AND_Gate
  and and_6 (and_6_out, register_4_bits_1_out1[0], ~register_4_bits_1_out1[1], ~register_4_bits_1_out1[2], ~register_4_bits_1_out1[3]);  // AND_Gate
  and and_7 (and_7_out, register_4_bits_1_out1[0], ~register_4_bits_1_out1[1], register_4_bits_1_out1[2], ~register_4_bits_1_out1[3], instruction[17]);  // AND_Gate
  and and_8 (and_8_out, register_4_bits_1_out1[0], ~register_4_bits_1_out1[1], ~register_4_bits_1_out1[2], register_4_bits_1_out1[3]);  // AND_Gate
  and and_9 (and_9_out, ~register_4_bits_1_out1[0], register_4_bits_1_out1[1], ~register_4_bits_1_out1[2], register_4_bits_1_out1[3]);  // AND_Gate
  and and_10 (and_10_out, ~register_4_bits_1_out1[0], ~register_4_bits_1_out1[1], register_4_bits_1_out1[2], register_4_bits_1_out1[3]);  // AND_Gate
  and and_11 (and_11_out, ~register_4_bits_1_out1[0], ~register_4_bits_1_out1[1], ~register_4_bits_1_out1[2], register_4_bits_1_out1[3], cmov_condition);  // AND_Gate
  and and_12 (and_12_out, ~register_4_bits_1_out1[0], ~register_4_bits_1_out1[1], register_4_bits_1_out1[2], ~register_4_bits_1_out1[3]);  // AND_Gate
  and and_13 (and_13_out, clock, and_1_out);
  and and_14 (and_14_out, clock, and_2_out);
  and and_15 (and_15_out, ~instruction[16], ~instruction[15]);  // AND_Gate
  and and_16 (and_16_out, ~instruction[17], instruction[16], ~instruction[15]);  // AND_Gate
  and and_17 (and_17_out, ~instruction[17], instruction[15], ~instruction[14]);  // AND_Gate
  and and_18 (and_18_out, ~instruction[17], ~instruction[16], instruction[15]);  // AND_Gate
  and and_19 (and_19_out, instruction[17], ~instruction[16], ~instruction[15]);  // AND_Gate
  not not_4 (not_4_out, st);
  or or_1 (or_1_out, and_13_out, and_14_out);
  and and_20 (and_20_out, ~instruction[17], ~instruction[16], instruction[15], ~instruction[14]);  // AND_Gate
  and and_21 (and_21_out, ~instruction[17], instruction[16], instruction[15], instruction[14]);  // AND_Gate
  and and_22 (and_22_out, instruction[17], instruction[16], instruction[15], ~instruction[14]);  // AND_Gate
  not not_5 (not_5_out, and_23_out);
  and and_23 (and_23_out, instruction[14], ~instruction[15], ~instruction[16], ~instruction[17], instruction[5]);  // AND_Gate
  and and_24 (and_24_out, instruction[17], ~instruction[16], ~instruction[15], instruction[14]);  // AND_Gate
  and and_25 (and_25_out, ~instruction[17], instruction[16], instruction[15], instruction[14]);  // AND_Gate
  or or_2 (and_29_out[2], and_25_out, and_19_out);
  and and_26 (and_26_out[3], ~instruction[17], ~instruction[16], ~instruction[15], instruction[14]);  // AND_Gate
  or or_3 (or_3_out, and_26_out[3], and_27_out);
  and and_27 (and_27_out, instruction[17], instruction[16], instruction[15], ~instruction[14]);  // AND_Gate
  assign controlled_buffer_7_out = st ? controlled_buffer_1_out : 4'bz;  // Controlled_Buffer controlled_buffer_7
  assign controlled_buffer_7_out = not_4_out ? instruction[9:6] : 4'bz;  // Controlled_Buffer controlled_buffer_8
  or or_4 (and_29_out[0], and_20_out, and_21_out, and_22_out, and_15_out);
  or or_5 (and_29_out[1], and_16_out, and_17_out, and_18_out, and_24_out);
  and and_28 (and_30_out[2], and_29_out[2], and_2_out);
  and and_29 (and_29_out[3], or_3_out, instruction[5]);
  and and_30 (and_30_out[0], and_29_out[0], not_5_out, and_2_out);
  and and_31 (and_30_out[1], and_29_out[1], and_2_out);
  and and_32 (and_30_out[3], and_29_out[3], and_2_out);
  Multiplexer #(.width(4), .enable("false")) multiplexer_1 (
    .in0(4'b0101), .in1(4'b0110), .out(multiplexer_1_out), .sel(instruction[4]));
  Multiplexer #(.select(2), .width(4), .enable("false")) multiplexer_2 (
    .in0(4'b0001), .in1(4'b0010), .in2(4'b0011), .in3(4'b0100), .out(multiplexer_2_out),
    .sel(instruction[5:4]));
  assign controlled_buffer_9_out = or_10_out ? 4'b1111 : 4'bz;  // Controlled_Buffer controlled_buffer_9
  assign controlled_buffer_9_out = or_6_out ? 4'b0110 : 4'bz;  // Controlled_Buffer controlled_buffer_10
  or or_6 (or_6_out, and_7_out, and_4_out);
  assign controlled_buffer_9_out = and_11_out ? 4'b1110 : 4'bz;  // Controlled_Buffer controlled_buffer_11
  assign controlled_buffer_9_out = and_9_out ? 4'b0100 : 4'bz;  // Controlled_Buffer controlled_buffer_12
  Multiplexer #(.width(4), .enable("false")) multiplexer_3 (
    .in0(controlled_buffer_1_out), .in1(controlled_buffer_7_out), .out(multiplexer_3_out), .sel(cmov));
  Multiplexer #(.width(4), .enable("false")) multiplexer_4 (
    .in0(controlled_buffer_7_out), .in1(controlled_buffer_1_out), .out(multiplexer_4_out), .sel(cmov));
  assign controlled_buffer_9_out = and_35_out ? and_30_out : 4'bz;  // Controlled_Buffer controlled_buffer_13
  Multiplexer #(.width(4)) multiplexer_5 (
    .in0(4'b1010), .in1(4'b1100), .out(controlled_buffer_9_out), .sel(instruction[4]), .en(and_8_out));
  assign controlled_buffer_9_out = and_12_out ? 4'b1011 : 4'bz;  // Controlled_Buffer controlled_buffer_14
  assign controlled_buffer_9_out = and_10_out ? 4'b1101 : 4'bz;  // Controlled_Buffer controlled_buffer_15
  Multiplexer #(.width(4), .enable("false")) multiplexer_6 (
    .in0(multiplexer_3_out), .in1(instruction[3:0]), .out(address_of_dest), .sel(or_7_out));
  or or_7 (or_7_out, read_stack, decrement_stack_ptr);
  Multiplexer #(.width(4), .enable("false")) multiplexer_7 (
    .in0(multiplexer_4_out), .in1(instruction[3:0]), .out(address_of_src1), .sel(or_8_out));
  or or_8 (or_8_out, increment_stack_ptr, write_to_stack);
  Multiplexer #(.width(4)) multiplexer_8 (
    .in0(multiplexer_2_out), .in1(multiplexer_1_out), .out(ALU_control_signal), .sel(instruction[14]),
    .en(or_9_out));
  or or_9 (or_9_out, and_33_out, and_36_out);
  and and_33 (and_33_out, and_34_out, or_11_out);
  and and_34 (and_34_out, and_29_out[0], ~and_29_out[1], ~and_29_out[2], ~and_29_out[3]);  // AND_Gate
  and and_35 (and_35_out, ~and_8_out, ~and_8_out, ~and_9_out, ~and_10_out, ~and_3_out, ~and_12_out, ~and_4_out, ~and_5_out, ~and_6_out, ~and_7_out, ~and_11_out);  // AND_Gate
  or or_10 (or_10_out, and_3_out, and_5_out, and_6_out);
  and and_36 (and_36_out, ~pc_write, ~or_11_out, ~decoder_1_out2);  // AND_Gate
  and and_37 (and_37_out, ~and_29_out[0], and_29_out[1], ~and_29_out[2], ~and_26_out[3]);  // AND_Gate
  Multiplexer #(.select(4), .width(4)) multiplexer_9 (
    .in3(4'b0001), .in4(4'b0010), .in5(4'b0011), .in6(4'b0100), .out(ALU_control_signal),
    .sel(instruction[17:14]), .en(ALU_input_control));  // open: in0, in1, in2, in7, in8, in9, in10, in11, in12, in13, in14, in15
  Decoder #(.select(4), .enable("false")) decoder_1 (
    .out2(decoder_1_out2), .out3(pc_write), .out4(decoder_1_out4), .out5(decoder_1_out5),
    .out6(decoder_1_out6), .out7(decoder_1_out7), .out8(decoder_1_out8), .out9(stack_op_state1),
    .out10(decoder_1_out10), .out11(decrement_stack_ptr), .out12(increment_stack_ptr),
    .out13(write_to_stack), .out14(decoder_1_out14), .out15(decoder_1_out15), .sel(controlled_buffer_2_out));  // open: out0, out1
  assign ALU_control_signal = pc_write ? 4'b0111 : 4'bz;  // Controlled_Buffer controlled_buffer_16
  buf buffer_1 (buffer_1_out, buffer_2_out);
  buf buffer_2 (buffer_2_out, clock);
  or or_11 (or_11_out, decoder_1_out14, decoder_1_out15);
  or or_12 (cmov, decoder_1_out8, decoder_1_out14);
  buf buffer_3 (buffer_3_out, buffer_4_out);
  buf buffer_4 (buffer_4_out, buffer_1_out);
  or or_13 (or_13_out, decoder_1_out5, decoder_1_out6);
  flip_flop flip_flop_1 (.in(instruction[13]), .clock(clock), .out(flip_flop_1_out));
  or or_14 (read_stack, decoder_1_out10, decoder_1_out4);
  flip_flop flip_flop_2 (.in(pc_write), .clock(buffer_3_out), .out(flip_flop_2_out));
  or or_15 (ALU_input_control, decoder_1_out2, and_37_out);
  and and_38 (jal, pc_write, flip_flop_1_out);
  flip_flop flip_flop_3 (.in(decoder_1_out7), .clock(buffer_3_out), .out(flip_flop_3_out));
  and and_39 (st, or_13_out, ~instruction[14]);  // AND_Gate
  or or_16 (we, jal, increment_stack_ptr, or_11_out, ld, decrement_stack_ptr, read_stack);
  and and_40 (ld, or_13_out, instruction[14]);
  or or_17 (lui, flip_flop_3_out, decoder_1_out7);
  assign pc_clock_signal = reset ? 1'b1 : 1'bz;  // Controlled_Buffer controlled_buffer_17
  assign pc_clock_signal = not_6_out ? and_41_out : 1'bz;  // Controlled_Buffer controlled_buffer_18
  not not_6 (not_6_out, reset);
  and and_41 (and_41_out, ~flip_flop_2_out, or_1_out);  // AND_Gate

  assign _6_bits_imm = instruction[5:0];
  assign _10_bits_imm = instruction[9:0];
  assign _13_bits_imm = instruction[12:0];
  assign address_of_src2 = instruction[3:0];
endmodule

module PC (
  input  [11:0] \input ,
  input  we,
  input  clock,
  input  reset,
  output [11:0] \output ,
  output [11:0] output_1
);

  wire buffer_1_out, buffer_2_out, buffer_3_out, buffer_4_out, buffer_5_out, buffer_6_out, buffer_7_out,
       buffer_8_out, buffer_9_out, buffer_10_out, buffer_11_out, buffer_12_out, buffer_13_out, buffer_14_out,
       buffer_15_out, buffer_16_out, buffer_17_out, buffer_18_out, buffer_19_out, buffer_20_out,
       buffer_21_out, buffer_22_out, buffer_23_out, buffer_24_out;
  wire [11:0] multiplexer_1_out, multiplexer_2_out, multiplexer_3_out;

  Multiplexer #(.width(12), .enable("false")) multiplexer_1 (
    .in0(output_1), .in1(\input ), .out(multiplexer_1_out), .sel(we));
  Multiplexer #(.width(12), .enable("false")) multiplexer_2 (
    .in0(multiplexer_1_out), .in1({12{1'b0}}), .out(multiplexer_2_out), .sel(reset));
  register_12_bit register_12_bit_1 (.in_1(multiplexer_2_out), .in_2(buffer_1_out), .out_3(\output ));
  buf buffer_1 (buffer_1_out, buffer_2_out);
  buf buffer_2 (buffer_2_out, buffer_3_out);
  buf buffer_3 (buffer_3_out, buffer_4_out);
  buf buffer_4 (buffer_4_out, buffer_5_out);
  buf buffer_5 (buffer_5_out, buffer_6_out);
  buf buffer_6 (buffer_6_out, buffer_7_out);
  buf buffer_7 (buffer_7_out, buffer_8_out);
  buf buffer_8 (buffer_8_out, buffer_9_out);
  buf buffer_9 (buffer_9_out, buffer_10_out);
  buf buffer_10 (buffer_10_out, buffer_11_out);
  buf buffer_11 (buffer_11_out, buffer_12_out);
  buf buffer_12 (buffer_12_out, buffer_13_out);
  buf buffer_13 (buffer_13_out, buffer_14_out);
  buf buffer_14 (buffer_14_out, buffer_15_out);
  buf buffer_15 (buffer_15_out, buffer_16_out);
  buf buffer_16 (buffer_16_out, buffer_17_out);
  buf buffer_17 (buffer_17_out, buffer_18_out);
  buf buffer_18 (buffer_18_out, buffer_19_out);
  buf buffer_19 (buffer_19_out, buffer_20_out);
  buf buffer_20 (buffer_20_out, buffer_21_out);
  buf buffer_21 (buffer_21_out, buffer_22_out);
  buf buffer_22 (buffer_22_out, buffer_23_out);
  buf buffer_23 (buffer_23_out, buffer_24_out);
  buf buffer_24 (buffer_24_out, clock);
  Multiplexer #(.width(12), .enable("false")) multiplexer_3 (
    .in0(\output ), .in1(\input ), .out(multiplexer_3_out), .sel(we));
  adder_12_bits adder_12_bits_1 (.input_1(multiplexer_3_out), .\output (output_1), .input_2(12'h1));  // open: c_out
endmodule

module right_shifter_1 (
  input  [17:0] input_1,
  input  l_a,
  output [17:0] \output 
);

  Multiplexer #(.enable("false")) multiplexer_1 (.in0(1'b0), .in1(input_1[17]), .out(\output [17]), .sel(l_a));

  assign \output [16:0] = input_1[17:1];
endmodule

module right_shifter_2 (
  input  [17:0] input_1,
  input  l_a,
  output [17:0] \output 
);

  Multiplexer #(.enable("false")) multiplexer_1 (.in0(1'b0), .in1(input_1[17]), .out(\output [17]), .sel(l_a));

  assign \output [16:0] = {\output [17], input_1[17:2]};
endmodule

module right_shifter_4 (
  input  [17:0] input_1,
  input  l_a,
  output [17:0] \output 
);

  Multiplexer #(.enable("false")) multiplexer_1 (.in0(1'b0), .in1(input_1[17]), .out(\output [17]), .sel(l_a));

  assign \output [16:0] = {{3{\output [17]}}, input_1[17:4]};
endmodule

module right_shifter_8 (
  input  [17:0] input_1,
  input  l_a,
  output [17:0] \output 
);

  Multiplexer #(.enable("false")) multiplexer_1 (.in0(1'b0), .in1(input_1[17]), .out(\output [17]), .sel(l_a));

  assign \output [16:0] = {{7{\output [17]}}, input_1[17:8]};
endmodule

module right_shifter_16 (
  input  [17:0] input_1,
  input  l_a,
  output [17:0] \output 
);

  Multiplexer #(.enable("false")) multiplexer_1 (.in0(1'b0), .in1(input_1[17]), .out(\output [17]), .sel(l_a));

  assign \output [16:0] = {{15{\output [17]}}, input_1[17:16]};
endmodule

module right_shifter_master (
  input  l_a,
  input  [17:0] input_1,
  input  [17:0] input_2,
  output [17:0] out_4
);

  wire or_1_out;
  wire [17:0] multiplexer_1_out, multiplexer_2_out, multiplexer_3_out, multiplexer_5_out, multiplexer_6_out,
       right_shifter_1_1_output, right_shifter_2_1_output, right_shifter_4_1_output,
       right_shifter_8_1_output, right_shifter_16_1_output;

  or or_1 (or_1_out, input_2[17], input_2[16], input_2[15], input_2[14], input_2[13], input_2[12], input_2[11], input_2[10], input_2[9], input_2[8], input_2[7], input_2[6], input_2[5]);
  Multiplexer #(.width(18), .enable("false")) multiplexer_1 (
    .in0(input_1), .in1(right_shifter_16_1_output), .out(multiplexer_1_out), .sel(input_2[4]));
  Multiplexer #(.width(18), .enable("false")) multiplexer_2 (
    .in0(multiplexer_1_out), .in1(right_shifter_8_1_output), .out(multiplexer_2_out), .sel(input_2[3]));
  Multiplexer #(.width(18), .enable("false")) multiplexer_3 (
    .in0(multiplexer_2_out), .in1(right_shifter_4_1_output), .out(multiplexer_3_out), .sel(input_2[2]));
  Multiplexer #(.width(18), .enable("false")) multiplexer_4 (
    .in0(multiplexer_6_out), .in1({18{1'b0}}), .out(out_4), .sel(or_1_out));
  right_shifter_16 right_shifter_16_1 (.input_1(input_1), .l_a(l_a), .\output (right_shifter_16_1_output));
  Multiplexer #(.width(18), .enable("false")) multiplexer_5 (
    .in0(multiplexer_3_out), .in1(right_shifter_2_1_output), .out(multiplexer_5_out), .sel(input_2[1]));
  Multiplexer #(.width(18), .enable("false")) multiplexer_6 (
    .in0(multiplexer_5_out), .in1(right_shifter_1_1_output), .out(multiplexer_6_out), .sel(input_2[0]));
  right_shifter_8 right_shifter_8_1 (.input_1(multiplexer_1_out), .l_a(l_a), .\output (right_shifter_8_1_output));
  right_shifter_4 right_shifter_4_1 (.input_1(multiplexer_2_out), .l_a(l_a), .\output (right_shifter_4_1_output));
  right_shifter_2 right_shifter_2_1 (.input_1(multiplexer_3_out), .l_a(l_a), .\output (right_shifter_2_1_output));
  right_shifter_1 right_shifter_1_1 (.input_1(multiplexer_5_out), .l_a(l_a), .\output (right_shifter_1_1_output));
endmodule

module flip_flop (
  input  in,
  input  clock,
  output out
);

  wire and_1_out, and_2_out, and_3_out, and_4_out, nor_1_out, nor_2_out, nor_3_out, not_1_out, not_2_out,
       not_3_out;

  not not_1 (not_1_out, clock);
  not not_2 (not_2_out, in);
  and and_1 (and_1_out, in, not_1_out);
  and and_2 (and_2_out, not_1_out, not_2_out);
  nor nor_1 (nor_1_out, and_1_out, nor_2_out);
  nor nor_2 (nor_2_out, nor_1_out, and_2_out);
  not not_3 (not_3_out, nor_2_out);
  and and_3 (and_3_out, nor_2_out, clock);
  and and_4 (and_4_out, clock, not_3_out);
  nor nor_3 (nor_3_out, and_3_out, out);
  nor nor_4 (out, nor_3_out, and_4_out);
endmodule

module register_3_bits (
  input  in3,
  input  in2,
  input  in1,
  input  clock,
  output out3,
  output out2,
  output out1
);

  flip_flop flip_flop_1 (.in(in2), .clock(clock), .out(out2));
  flip_flop flip_flop_2 (.in(in3), .clock(clock), .out(out3));
  flip_flop flip_flop_3 (.in(in1), .clock(clock), .out(out1));
endmodule

module register_4_bits (
  input  in4,
  input  in3,
  input  in2,
  input  in1,
  input  clock,
  output out4,
  output out3,
  output out2,
  output out1
);

  flip_flop flip_flop_1 (.in(in4), .clock(clock), .out(out4));
  flip_flop flip_flop_2 (.in(in3), .clock(clock), .out(out3));
  flip_flop flip_flop_3 (.in(in2), .clock(clock), .out(out2));
  flip_flop flip_flop_4 (.in(in1), .clock(clock), .out(out1));
endmodule

module register_12_bit (
  input  [11:0] in_1,
  input  in_2,
  output [11:0] out_3
);

  flip_flop flip_flop_1 (.in(in_1[10]), .clock(in_2), .out(out_3[10]));
  flip_flop flip_flop_2 (.in(in_1[11]), .clock(in_2), .out(out_3[11]));
  flip_flop flip_flop_3 (.in(in_1[9]), .clock(in_2), .out(out_3[9]));
  flip_flop flip_flop_4 (.in(in_1[8]), .clock(in_2), .out(out_3[8]));
  flip_flop flip_flop_5 (.in(in_1[7]), .clock(in_2), .out(out_3[7]));
  flip_flop flip_flop_6 (.in(in_1[6]), .clock(in_2), .out(out_3[6]));
  flip_flop flip_flop_7 (.in(in_1[5]), .clock(in_2), .out(out_3[5]));
  flip_flop flip_flop_8 (.in(in_1[4]), .clock(in_2), .out(out_3[4]));
  flip_flop flip_flop_9 (.in(in_1[2]), .clock(in_2), .out(out_3[2]));
  flip_flop flip_flop_10 (.in(in_1[3]), .clock(in_2), .out(out_3[3]));
  flip_flop flip_flop_11 (.in(in_1[1]), .clock(in_2), .out(out_3[1]));
  flip_flop flip_flop_12 (.in(in_1[0]), .clock(in_2), .out(out_3[0]));
endmodule

module register_18_bit (
  input  [17:0] in_1,
  input  in_2,
  output [17:0] out_3
);

  flip_flop flip_flop_1 (.in(in_1[17]), .clock(in_2), .out(out_3[17]));
  flip_flop flip_flop_2 (.in(in_1[16]), .clock(in_2), .out(out_3[16]));
  flip_flop flip_flop_3 (.in(in_1[15]), .clock(in_2), .out(out_3[15]));
  flip_flop flip_flop_4 (.in(in_1[14]), .clock(in_2), .out(out_3[14]));
  flip_flop flip_flop_5 (.in(in_1[13]), .clock(in_2), .out(out_3[13]));
  flip_flop flip_flop_6 (.in(in_1[12]), .clock(in_2), .out(out_3[12]));
  flip_flop flip_flop_7 (.in(in_1[11]), .clock(in_2), .out(out_3[11]));
  flip_flop flip_flop_8 (.in(in_1[10]), .clock(in_2), .out(out_3[10]));
  flip_flop flip_flop_9 (.in(in_1[9]), .clock(in_2), .out(out_3[9]));
  flip_flop flip_flop_10 (.in(in_1[8]), .clock(in_2), .out(out_3[8]));
  flip_flop flip_flop_11 (.in(in_1[7]), .clock(in_2), .out(out_3[7]));
  flip_flop flip_flop_12 (.in(in_1[6]), .clock(in_2), .out(out_3[6]));
  flip_flop flip_flop_13 (.in(in_1[5]), .clock(in_2), .out(out_3[5]));
  flip_flop flip_flop_14 (.in(in_1[4]), .clock(in_2), .out(out_3[4]));
  flip_flop flip_flop_15 (.in(in_1[2]), .clock(in_2), .out(out_3[2]));
  flip_flop flip_flop_16 (.in(in_1[3]), .clock(in_2), .out(out_3[3]));
  flip_flop flip_flop_17 (.in(in_1[1]), .clock(in_2), .out(out_3[1]));
  flip_flop flip_flop_18 (.in(in_1[0]), .clock(in_2), .out(out_3[0]));
endmodule

module adder_1_bit_wo_carry (
  input  input_1,
  input  input_2,
  output carry_out,
  output \output 
);

  and and_1 (carry_out, input_1, input_2);
  xor xor_1 (\output , input_1, input_2);
endmodule

module adder_1_bit (
  input  input_1,
  input  input_2,
  input  carry_in,
  output carry_out,
  output \output 
);

  wire and_1_out, and_2_out, and_3_out, and_4_out, and_5_out, and_6_out, and_7_out, and_8_out;

  and and_1 (and_1_out, ~input_1, input_2, carry_in);  // AND_Gate
  and and_2 (and_2_out, input_1, ~input_2, carry_in);  // AND_Gate
  and and_3 (and_3_out, input_1, input_2, ~carry_in);  // AND_Gate
  and and_4 (and_4_out, input_1, input_2, carry_in);
  and and_5 (and_5_out, ~input_1, ~input_2, carry_in);  // AND_Gate
  and and_6 (and_6_out, input_1, ~input_2, ~carry_in);  // AND_Gate
  and and_7 (and_7_out, ~input_1, input_2, ~carry_in);  // AND_Gate
  and and_8 (and_8_out, input_1, input_2, carry_in);
  or or_1 (carry_out, and_1_out, and_2_out, and_3_out, and_4_out);
  or or_2 (\output , and_5_out, and_6_out, and_7_out, and_8_out);
endmodule

module adder_6_bits (
  input  [5:0] input_1,
  input  [5:0] input_2,
  output c_out,
  output [5:0] \output 
);

  wire adder_1_bit_2_carry_out, adder_1_bit_3_carry_out, adder_1_bit_4_carry_out, adder_1_bit_5_carry_out,
       adder_1_bit_wo_carry_1_carry_out;

  adder_1_bit adder_1_bit_1 (
    .input_1(input_1[5]), .input_2(input_2[5]), .carry_in(adder_1_bit_2_carry_out), .carry_out(c_out),
    .\output (\output [5]));
  adder_1_bit adder_1_bit_2 (
    .input_1(input_1[4]), .input_2(input_2[4]), .carry_in(adder_1_bit_3_carry_out),
    .carry_out(adder_1_bit_2_carry_out), .\output (\output [4]));
  adder_1_bit adder_1_bit_3 (
    .input_1(input_1[3]), .input_2(input_2[3]), .carry_in(adder_1_bit_4_carry_out),
    .carry_out(adder_1_bit_3_carry_out), .\output (\output [3]));
  adder_1_bit adder_1_bit_4 (
    .input_1(input_1[2]), .input_2(input_2[2]), .carry_in(adder_1_bit_5_carry_out),
    .carry_out(adder_1_bit_4_carry_out), .\output (\output [2]));
  adder_1_bit adder_1_bit_5 (
    .input_1(input_1[1]), .input_2(input_2[1]), .carry_in(adder_1_bit_wo_carry_1_carry_out),
    .carry_out(adder_1_bit_5_carry_out), .\output (\output [1]));
  adder_1_bit_wo_carry adder_1_bit_wo_carry_1 (
    .input_1(input_1[0]), .input_2(input_2[0]), .carry_out(adder_1_bit_wo_carry_1_carry_out),
    .\output (\output [0]));
endmodule

module adder_6_bits_w_clock (
  input  [5:0] input_1,
  input  clock,
  input  [5:0] input_2,
  output c_out,
  output [5:0] \output 
);

  wire adder_1_bit_1_carry_out, adder_1_bit_1_output, adder_1_bit_2_carry_out, adder_1_bit_2_output,
       adder_1_bit_3_carry_out, adder_1_bit_3_output, adder_1_bit_4_carry_out, adder_1_bit_4_output,
       adder_1_bit_5_carry_out, adder_1_bit_5_output, adder_1_bit_wo_carry_1_carry_out,
       adder_1_bit_wo_carry_1_output;

  and and_1 (\output [0], adder_1_bit_wo_carry_1_output, clock);
  and and_2 (\output [1], adder_1_bit_5_output, clock);
  and and_3 (\output [2], adder_1_bit_4_output, clock);
  and and_4 (\output [3], adder_1_bit_3_output, clock);
  and and_5 (\output [4], adder_1_bit_2_output, clock);
  and and_6 (\output [5], adder_1_bit_1_output, clock);
  and and_7 (c_out, clock, adder_1_bit_1_carry_out);
  adder_1_bit adder_1_bit_1 (
    .input_1(input_1[5]), .input_2(input_2[5]), .carry_in(adder_1_bit_2_carry_out),
    .carry_out(adder_1_bit_1_carry_out), .\output (adder_1_bit_1_output));
  adder_1_bit adder_1_bit_2 (
    .input_1(input_1[4]), .input_2(input_2[4]), .carry_in(adder_1_bit_3_carry_out),
    .carry_out(adder_1_bit_2_carry_out), .\output (adder_1_bit_2_output));
  adder_1_bit adder_1_bit_3 (
    .input_1(input_1[3]), .input_2(input_2[3]), .carry_in(adder_1_bit_4_carry_out),
    .carry_out(adder_1_bit_3_carry_out), .\output (adder_1_bit_3_output));
  adder_1_bit adder_1_bit_4 (
    .input_1(input_1[2]), .input_2(input_2[2]), .carry_in(adder_1_bit_5_carry_out),
    .carry_out(adder_1_bit_4_carry_out), .\output (adder_1_bit_4_output));
  adder_1_bit adder_1_bit_5 (
    .input_1(input_1[1]), .input_2(input_2[1]), .carry_in(adder_1_bit_wo_carry_1_carry_out),
    .carry_out(adder_1_bit_5_carry_out), .\output (adder_1_bit_5_output));
  adder_1_bit_wo_carry adder_1_bit_wo_carry_1 (
    .input_1(input_1[0]), .input_2(input_2[0]), .carry_out(adder_1_bit_wo_carry_1_carry_out),
    .\output (adder_1_bit_wo_carry_1_output));
endmodule

module adder_9_bits (
  input  [8:0] input_1,
  input  [8:0] input_2,
  output [8:0] \output ,
  output c_out
);

  wire adder_1_bit_2_carry_out, adder_1_bit_3_carry_out, adder_1_bit_4_carry_out, adder_1_bit_5_carry_out,
       adder_1_bit_6_carry_out, adder_1_bit_7_carry_out, adder_1_bit_8_carry_out,
       adder_1_bit_wo_carry_1_carry_out;

  adder_1_bit adder_1_bit_1 (
    .input_1(input_1[8]), .input_2(input_2[8]), .carry_in(adder_1_bit_2_carry_out), .carry_out(c_out),
    .\output (\output [8]));
  adder_1_bit adder_1_bit_2 (
    .input_1(input_1[7]), .input_2(input_2[7]), .carry_in(adder_1_bit_3_carry_out),
    .carry_out(adder_1_bit_2_carry_out), .\output (\output [7]));
  adder_1_bit adder_1_bit_3 (
    .input_1(input_1[6]), .input_2(input_2[6]), .carry_in(adder_1_bit_4_carry_out),
    .carry_out(adder_1_bit_3_carry_out), .\output (\output [6]));
  adder_1_bit adder_1_bit_4 (
    .input_1(input_1[5]), .input_2(input_2[5]), .carry_in(adder_1_bit_5_carry_out),
    .carry_out(adder_1_bit_4_carry_out), .\output (\output [5]));
  adder_1_bit adder_1_bit_5 (
    .input_1(input_1[4]), .input_2(input_2[4]), .carry_in(adder_1_bit_6_carry_out),
    .carry_out(adder_1_bit_5_carry_out), .\output (\output [4]));
  adder_1_bit adder_1_bit_6 (
    .input_1(input_1[3]), .input_2(input_2[3]), .carry_in(adder_1_bit_7_carry_out),
    .carry_out(adder_1_bit_6_carry_out), .\output (\output [3]));
  adder_1_bit adder_1_bit_7 (
    .input_1(input_1[2]), .input_2(input_2[2]), .carry_in(adder_1_bit_8_carry_out),
    .carry_out(adder_1_bit_7_carry_out), .\output (\output [2]));
  adder_1_bit adder_1_bit_8 (
    .input_1(input_1[1]), .input_2(input_2[1]), .carry_in(adder_1_bit_wo_carry_1_carry_out),
    .carry_out(adder_1_bit_8_carry_out), .\output (\output [1]));
  adder_1_bit_wo_carry adder_1_bit_wo_carry_1 (
    .input_1(input_1[0]), .input_2(input_2[0]), .carry_out(adder_1_bit_wo_carry_1_carry_out),
    .\output (\output [0]));
endmodule

module adder_9_bits_w_clock (
  input  [8:0] input_1,
  input  clock,
  input  [8:0] input_2,
  output c_out,
  output [8:0] \output 
);

  wire adder_1_bit_1_carry_out, adder_1_bit_1_output, adder_1_bit_2_carry_out, adder_1_bit_2_output,
       adder_1_bit_3_carry_out, adder_1_bit_3_output, adder_1_bit_4_carry_out, adder_1_bit_4_output,
       adder_1_bit_5_carry_out, adder_1_bit_5_output, adder_1_bit_6_carry_out, adder_1_bit_6_output,
       adder_1_bit_7_carry_out, adder_1_bit_7_output, adder_1_bit_8_carry_out, adder_1_bit_8_output,
       adder_1_bit_wo_carry_1_carry_out, adder_1_bit_wo_carry_1_output;

  and and_1 (\output [0], adder_1_bit_wo_carry_1_output, clock);
  and and_2 (\output [1], adder_1_bit_8_output, clock);
  and and_3 (\output [2], adder_1_bit_7_output, clock);
  and and_4 (\output [3], adder_1_bit_5_output, clock);
  and and_5 (\output [4], adder_1_bit_6_output, clock);
  and and_6 (\output [5], adder_1_bit_4_output, clock);
  and and_7 (\output [6], adder_1_bit_3_output, clock);
  and and_8 (\output [7], adder_1_bit_2_output, clock);
  and and_9 (\output [8], adder_1_bit_1_output, clock);
  and and_10 (c_out, clock, adder_1_bit_1_carry_out);
  adder_1_bit adder_1_bit_1 (
    .input_1(input_1[8]), .input_2(input_2[8]), .carry_in(adder_1_bit_2_carry_out),
    .carry_out(adder_1_bit_1_carry_out), .\output (adder_1_bit_1_output));
  adder_1_bit adder_1_bit_2 (
    .input_1(input_1[7]), .input_2(input_2[7]), .carry_in(adder_1_bit_3_carry_out),
    .carry_out(adder_1_bit_2_carry_out), .\output (adder_1_bit_2_output));
  adder_1_bit adder_1_bit_3 (
    .input_1(input_1[6]), .input_2(input_2[6]), .carry_in(adder_1_bit_4_carry_out),
    .carry_out(adder_1_bit_3_carry_out), .\output (adder_1_bit_3_output));
  adder_1_bit adder_1_bit_4 (
    .input_1(input_1[5]), .input_2(input_2[5]), .carry_in(adder_1_bit_6_carry_out),
    .carry_out(adder_1_bit_4_carry_out), .\output (adder_1_bit_4_output));
  adder_1_bit adder_1_bit_5 (
    .input_1(input_1[3]), .input_2(input_2[3]), .carry_in(adder_1_bit_7_carry_out),
    .carry_out(adder_1_bit_5_carry_out), .\output (adder_1_bit_5_output));
  adder_1_bit adder_1_bit_6 (
    .input_1(input_1[4]), .input_2(input_2[4]), .carry_in(adder_1_bit_5_carry_out),
    .carry_out(adder_1_bit_6_carry_out), .\output (adder_1_bit_6_output));
  adder_1_bit adder_1_bit_7 (
    .input_1(input_1[2]), .input_2(input_2[2]), .carry_in(adder_1_bit_8_carry_out),
    .carry_out(adder_1_bit_7_carry_out), .\output (adder_1_bit_7_output));
  adder_1_bit adder_1_bit_8 (
    .input_1(input_1[1]), .input_2(input_2[1]), .carry_in(adder_1_bit_wo_carry_1_carry_out),
    .carry_out(adder_1_bit_8_carry_out), .\output (adder_1_bit_8_output));
  adder_1_bit_wo_carry adder_1_bit_wo_carry_1 (
    .input_1(input_1[0]), .input_2(input_2[0]), .carry_out(adder_1_bit_wo_carry_1_carry_out),
    .\output (adder_1_bit_wo_carry_1_output));
endmodule

module adder_10_bits (
  input  [9:0] input_1,
  input  [9:0] input_2,
  output [9:0] \output ,
  output c_out
);

  wire adder_1_bit_2_carry_out, adder_1_bit_3_carry_out, adder_1_bit_4_carry_out, adder_1_bit_5_carry_out,
       adder_1_bit_6_carry_out, adder_1_bit_7_carry_out, adder_1_bit_8_carry_out, adder_1_bit_9_carry_out,
       adder_1_bit_wo_carry_1_carry_out;

  adder_1_bit adder_1_bit_1 (
    .input_1(input_1[9]), .input_2(input_2[9]), .carry_in(adder_1_bit_2_carry_out), .carry_out(c_out),
    .\output (\output [9]));
  adder_1_bit adder_1_bit_2 (
    .input_1(input_1[8]), .input_2(input_2[8]), .carry_in(adder_1_bit_3_carry_out),
    .carry_out(adder_1_bit_2_carry_out), .\output (\output [8]));
  adder_1_bit adder_1_bit_3 (
    .input_1(input_1[7]), .input_2(input_2[7]), .carry_in(adder_1_bit_5_carry_out),
    .carry_out(adder_1_bit_3_carry_out), .\output (\output [7]));
  adder_1_bit adder_1_bit_4 (
    .input_1(input_1[5]), .input_2(input_2[5]), .carry_in(adder_1_bit_6_carry_out),
    .carry_out(adder_1_bit_4_carry_out), .\output (\output [5]));
  adder_1_bit adder_1_bit_5 (
    .input_1(input_1[6]), .input_2(input_2[6]), .carry_in(adder_1_bit_4_carry_out),
    .carry_out(adder_1_bit_5_carry_out), .\output (\output [6]));
  adder_1_bit adder_1_bit_6 (
    .input_1(input_1[4]), .input_2(input_2[4]), .carry_in(adder_1_bit_8_carry_out),
    .carry_out(adder_1_bit_6_carry_out), .\output (\output [4]));
  adder_1_bit adder_1_bit_7 (
    .input_1(input_1[2]), .input_2(input_2[2]), .carry_in(adder_1_bit_9_carry_out),
    .carry_out(adder_1_bit_7_carry_out), .\output (\output [2]));
  adder_1_bit adder_1_bit_8 (
    .input_1(input_1[3]), .input_2(input_2[3]), .carry_in(adder_1_bit_7_carry_out),
    .carry_out(adder_1_bit_8_carry_out), .\output (\output [3]));
  adder_1_bit adder_1_bit_9 (
    .input_1(input_1[1]), .input_2(input_2[1]), .carry_in(adder_1_bit_wo_carry_1_carry_out),
    .carry_out(adder_1_bit_9_carry_out), .\output (\output [1]));
  adder_1_bit_wo_carry adder_1_bit_wo_carry_1 (
    .input_1(input_1[0]), .input_2(input_2[0]), .carry_out(adder_1_bit_wo_carry_1_carry_out),
    .\output (\output [0]));
endmodule

module adder_10_bits_w_clock (
  input  [9:0] input_1,
  input  clock,
  input  [9:0] input_2,
  output c_out,
  output [9:0] \output 
);

  wire adder_1_bit_1_carry_out, adder_1_bit_1_output, adder_1_bit_2_carry_out, adder_1_bit_2_output,
       adder_1_bit_3_carry_out, adder_1_bit_3_output, adder_1_bit_4_carry_out, adder_1_bit_4_output,
       adder_1_bit_5_carry_out, adder_1_bit_5_output, adder_1_bit_6_carry_out, adder_1_bit_6_output,
       adder_1_bit_7_carry_out, adder_1_bit_7_output, adder_1_bit_8_carry_out, adder_1_bit_8_output,
       adder_1_bit_9_carry_out, adder_1_bit_9_output, adder_1_bit_wo_carry_1_carry_out,
       adder_1_bit_wo_carry_1_output;

  and and_1 (\output [0], adder_1_bit_wo_carry_1_output, clock);
  and and_2 (\output [1], adder_1_bit_9_output, clock);
  and and_3 (\output [2], adder_1_bit_8_output, clock);
  and and_4 (\output [3], adder_1_bit_6_output, clock);
  and and_5 (\output [4], adder_1_bit_7_output, clock);
  and and_6 (\output [5], adder_1_bit_4_output, clock);
  and and_7 (\output [6], adder_1_bit_5_output, clock);
  and and_8 (\output [7], adder_1_bit_3_output, clock);
  and and_9 (\output [8], adder_1_bit_2_output, clock);
  and and_10 (\output [9], adder_1_bit_1_output, clock);
  and and_11 (c_out, clock, adder_1_bit_1_carry_out);
  adder_1_bit adder_1_bit_1 (
    .input_1(input_1[9]), .input_2(input_2[9]), .carry_in(adder_1_bit_2_carry_out),
    .carry_out(adder_1_bit_1_carry_out), .\output (adder_1_bit_1_output));
  adder_1_bit adder_1_bit_2 (
    .input_1(input_1[8]), .input_2(input_2[8]), .carry_in(adder_1_bit_3_carry_out),
    .carry_out(adder_1_bit_2_carry_out), .\output (adder_1_bit_2_output));
  adder_1_bit adder_1_bit_3 (
    .input_1(input_1[7]), .input_2(input_2[7]), .carry_in(adder_1_bit_5_carry_out),
    .carry_out(adder_1_bit_3_carry_out), .\output (adder_1_bit_3_output));
  adder_1_bit adder_1_bit_4 (
    .input_1(input_1[5]), .input_2(input_2[5]), .carry_in(adder_1_bit_7_carry_out),
    .carry_out(adder_1_bit_4_carry_out), .\output (adder_1_bit_4_output));
  adder_1_bit adder_1_bit_5 (
    .input_1(input_1[6]), .input_2(input_2[6]), .carry_in(adder_1_bit_4_carry_out),
    .carry_out(adder_1_bit_5_carry_out), .\output (adder_1_bit_5_output));
  adder_1_bit adder_1_bit_6 (
    .input_1(input_1[3]), .input_2(input_2[3]), .carry_in(adder_1_bit_8_carry_out),
    .carry_out(adder_1_bit_6_carry_out), .\output (adder_1_bit_6_output));
  adder_1_bit adder_1_bit_7 (
    .input_1(input_1[4]), .input_2(input_2[4]), .carry_in(adder_1_bit_6_carry_out),
    .carry_out(adder_1_bit_7_carry_out), .\output (adder_1_bit_7_output));
  adder_1_bit adder_1_bit_8 (
    .input_1(input_1[2]), .input_2(input_2[2]), .carry_in(adder_1_bit_9_carry_out),
    .carry_out(adder_1_bit_8_carry_out), .\output (adder_1_bit_8_output));
  adder_1_bit adder_1_bit_9 (
    .input_1(input_1[1]), .input_2(input_2[1]), .carry_in(adder_1_bit_wo_carry_1_carry_out),
    .carry_out(adder_1_bit_9_carry_out), .\output (adder_1_bit_9_output));
  adder_1_bit_wo_carry adder_1_bit_wo_carry_1 (
    .input_1(input_1[0]), .input_2(input_2[0]), .carry_out(adder_1_bit_wo_carry_1_carry_out),
    .\output (adder_1_bit_wo_carry_1_output));
endmodule

module adder_12_bits (
  input  [11:0] input_1,
  input  [11:0] input_2,
  output c_out,
  output [11:0] \output 
);

  wire adder_1_bit_1_carry_out, adder_1_bit_3_carry_out, adder_1_bit_4_carry_out, adder_1_bit_5_carry_out,
       adder_1_bit_6_carry_out, adder_1_bit_7_carry_out, adder_1_bit_8_carry_out, adder_1_bit_9_carry_out,
       adder_1_bit_10_carry_out, adder_1_bit_11_carry_out, adder_1_bit_wo_carry_1_carry_out;

  adder_1_bit adder_1_bit_1 (
    .input_1(input_1[10]), .input_2(input_2[10]), .carry_in(adder_1_bit_3_carry_out),
    .carry_out(adder_1_bit_1_carry_out), .\output (\output [10]));
  adder_1_bit adder_1_bit_2 (
    .input_1(input_1[11]), .input_2(input_2[11]), .carry_in(adder_1_bit_1_carry_out), .carry_out(c_out),
    .\output (\output [11]));
  adder_1_bit adder_1_bit_3 (
    .input_1(input_1[9]), .input_2(input_2[9]), .carry_in(adder_1_bit_4_carry_out),
    .carry_out(adder_1_bit_3_carry_out), .\output (\output [9]));
  adder_1_bit adder_1_bit_4 (
    .input_1(input_1[8]), .input_2(input_2[8]), .carry_in(adder_1_bit_5_carry_out),
    .carry_out(adder_1_bit_4_carry_out), .\output (\output [8]));
  adder_1_bit adder_1_bit_5 (
    .input_1(input_1[7]), .input_2(input_2[7]), .carry_in(adder_1_bit_6_carry_out),
    .carry_out(adder_1_bit_5_carry_out), .\output (\output [7]));
  adder_1_bit adder_1_bit_6 (
    .input_1(input_1[6]), .input_2(input_2[6]), .carry_in(adder_1_bit_7_carry_out),
    .carry_out(adder_1_bit_6_carry_out), .\output (\output [6]));
  adder_1_bit adder_1_bit_7 (
    .input_1(input_1[5]), .input_2(input_2[5]), .carry_in(adder_1_bit_8_carry_out),
    .carry_out(adder_1_bit_7_carry_out), .\output (\output [5]));
  adder_1_bit adder_1_bit_8 (
    .input_1(input_1[4]), .input_2(input_2[4]), .carry_in(adder_1_bit_10_carry_out),
    .carry_out(adder_1_bit_8_carry_out), .\output (\output [4]));
  adder_1_bit adder_1_bit_9 (
    .input_1(input_1[2]), .input_2(input_2[2]), .carry_in(adder_1_bit_11_carry_out),
    .carry_out(adder_1_bit_9_carry_out), .\output (\output [2]));
  adder_1_bit adder_1_bit_10 (
    .input_1(input_1[3]), .input_2(input_2[3]), .carry_in(adder_1_bit_9_carry_out),
    .carry_out(adder_1_bit_10_carry_out), .\output (\output [3]));
  adder_1_bit adder_1_bit_11 (
    .input_1(input_1[1]), .input_2(input_2[1]), .carry_in(adder_1_bit_wo_carry_1_carry_out),
    .carry_out(adder_1_bit_11_carry_out), .\output (\output [1]));
  adder_1_bit_wo_carry adder_1_bit_wo_carry_1 (
    .input_1(input_1[0]), .input_2(input_2[0]), .carry_out(adder_1_bit_wo_carry_1_carry_out),
    .\output (\output [0]));
endmodule

module adder_12_bits_w_clock (
  input  [11:0] input_1,
  input  clock,
  input  [11:0] input_2,
  output c_out,
  output [11:0] \output 
);

  wire adder_1_bit_1_carry_out, adder_1_bit_1_output, adder_1_bit_2_carry_out, adder_1_bit_2_output,
       adder_1_bit_3_carry_out, adder_1_bit_3_output, adder_1_bit_4_carry_out, adder_1_bit_4_output,
       adder_1_bit_5_carry_out, adder_1_bit_5_output, adder_1_bit_6_carry_out, adder_1_bit_6_output,
       adder_1_bit_7_carry_out, adder_1_bit_7_output, adder_1_bit_8_carry_out, adder_1_bit_8_output,
       adder_1_bit_9_carry_out, adder_1_bit_9_output, adder_1_bit_10_carry_out, adder_1_bit_10_output,
       adder_1_bit_11_carry_out, adder_1_bit_11_output, adder_1_bit_wo_carry_1_carry_out,
       adder_1_bit_wo_carry_1_output;

  and and_1 (\output [0], adder_1_bit_wo_carry_1_output, clock);
  and and_2 (\output [1], adder_1_bit_11_output, clock);
  and and_3 (\output [2], adder_1_bit_10_output, clock);
  and and_4 (\output [3], adder_1_bit_9_output, clock);
  and and_5 (\output [4], adder_1_bit_8_output, clock);
  and and_6 (\output [5], adder_1_bit_7_output, clock);
  and and_7 (\output [6], adder_1_bit_6_output, clock);
  and and_8 (\output [7], adder_1_bit_5_output, clock);
  and and_9 (\output [8], adder_1_bit_4_output, clock);
  and and_10 (\output [9], adder_1_bit_3_output, clock);
  and and_11 (\output [10], adder_1_bit_2_output, clock);
  and and_12 (\output [11], adder_1_bit_1_output, clock);
  and and_13 (c_out, clock, adder_1_bit_1_carry_out);
  adder_1_bit adder_1_bit_1 (
    .input_1(input_1[11]), .input_2(input_2[11]), .carry_in(adder_1_bit_2_carry_out),
    .carry_out(adder_1_bit_1_carry_out), .\output (adder_1_bit_1_output));
  adder_1_bit adder_1_bit_2 (
    .input_1(input_1[10]), .input_2(input_2[10]), .carry_in(adder_1_bit_3_carry_out),
    .carry_out(adder_1_bit_2_carry_out), .\output (adder_1_bit_2_output));
  adder_1_bit adder_1_bit_3 (
    .input_1(input_1[9]), .input_2(input_2[9]), .carry_in(adder_1_bit_4_carry_out),
    .carry_out(adder_1_bit_3_carry_out), .\output (adder_1_bit_3_output));
  adder_1_bit adder_1_bit_4 (
    .input_1(input_1[8]), .input_2(input_2[8]), .carry_in(adder_1_bit_5_carry_out),
    .carry_out(adder_1_bit_4_carry_out), .\output (adder_1_bit_4_output));
  adder_1_bit adder_1_bit_5 (
    .input_1(input_1[7]), .input_2(input_2[7]), .carry_in(adder_1_bit_6_carry_out),
    .carry_out(adder_1_bit_5_carry_out), .\output (adder_1_bit_5_output));
  adder_1_bit adder_1_bit_6 (
    .input_1(input_1[6]), .input_2(input_2[6]), .carry_in(adder_1_bit_7_carry_out),
    .carry_out(adder_1_bit_6_carry_out), .\output (adder_1_bit_6_output));
  adder_1_bit adder_1_bit_7 (
    .input_1(input_1[5]), .input_2(input_2[5]), .carry_in(adder_1_bit_8_carry_out),
    .carry_out(adder_1_bit_7_carry_out), .\output (adder_1_bit_7_output));
  adder_1_bit adder_1_bit_8 (
    .input_1(input_1[4]), .input_2(input_2[4]), .carry_in(adder_1_bit_9_carry_out),
    .carry_out(adder_1_bit_8_carry_out), .\output (adder_1_bit_8_output));
  adder_1_bit adder_1_bit_9 (
    .input_1(input_1[3]), .input_2(input_2[3]), .carry_in(adder_1_bit_10_carry_out),
    .carry_out(adder_1_bit_9_carry_out), .\output (adder_1_bit_9_output));
  adder_1_bit adder_1_bit_10 (
    .input_1(input_1[2]), .input_2(input_2[2]), .carry_in(adder_1_bit_11_carry_out),
    .carry_out(adder_1_bit_10_carry_out), .\output (adder_1_bit_10_output));
  adder_1_bit adder_1_bit_11 (
    .input_1(input_1[1]), .input_2(input_2[1]), .carry_in(adder_1_bit_wo_carry_1_carry_out),
    .carry_out(adder_1_bit_11_carry_out), .\output (adder_1_bit_11_output));
  adder_1_bit_wo_carry adder_1_bit_wo_carry_1 (
    .input_1(input_1[0]), .input_2(input_2[0]), .carry_out(adder_1_bit_wo_carry_1_carry_out),
    .\output (adder_1_bit_wo_carry_1_output));
endmodule

module adder_13_bits (
  input  [12:0] input_1,
  input  [12:0] input_2,
  output c_out,
  output [12:0] \output 
);

  wire adder_1_bit_2_carry_out, adder_1_bit_3_carry_out, adder_1_bit_4_carry_out, adder_1_bit_5_carry_out,
       adder_1_bit_6_carry_out, adder_1_bit_7_carry_out, adder_1_bit_8_carry_out, adder_1_bit_9_carry_out,
       adder_1_bit_10_carry_out, adder_1_bit_11_carry_out, adder_1_bit_12_carry_out,
       adder_1_bit_wo_carry_1_carry_out;

  adder_1_bit adder_1_bit_1 (
    .input_1(input_1[12]), .input_2(input_2[12]), .carry_in(adder_1_bit_2_carry_out), .carry_out(c_out),
    .\output (\output [12]));
  adder_1_bit adder_1_bit_2 (
    .input_1(input_1[11]), .input_2(input_2[11]), .carry_in(adder_1_bit_3_carry_out),
    .carry_out(adder_1_bit_2_carry_out), .\output (\output [11]));
  adder_1_bit adder_1_bit_3 (
    .input_1(input_1[10]), .input_2(input_2[10]), .carry_in(adder_1_bit_4_carry_out),
    .carry_out(adder_1_bit_3_carry_out), .\output (\output [10]));
  adder_1_bit adder_1_bit_4 (
    .input_1(input_1[9]), .input_2(input_2[9]), .carry_in(adder_1_bit_5_carry_out),
    .carry_out(adder_1_bit_4_carry_out), .\output (\output [9]));
  adder_1_bit adder_1_bit_5 (
    .input_1(input_1[8]), .input_2(input_2[8]), .carry_in(adder_1_bit_6_carry_out),
    .carry_out(adder_1_bit_5_carry_out), .\output (\output [8]));
  adder_1_bit adder_1_bit_6 (
    .input_1(input_1[7]), .input_2(input_2[7]), .carry_in(adder_1_bit_7_carry_out),
    .carry_out(adder_1_bit_6_carry_out), .\output (\output [7]));
  adder_1_bit adder_1_bit_7 (
    .input_1(input_1[6]), .input_2(input_2[6]), .carry_in(adder_1_bit_8_carry_out),
    .carry_out(adder_1_bit_7_carry_out), .\output (\output [6]));
  adder_1_bit adder_1_bit_8 (
    .input_1(input_1[5]), .input_2(input_2[5]), .carry_in(adder_1_bit_9_carry_out),
    .carry_out(adder_1_bit_8_carry_out), .\output (\output [5]));
  adder_1_bit adder_1_bit_9 (
    .input_1(input_1[4]), .input_2(input_2[4]), .carry_in(adder_1_bit_11_carry_out),
    .carry_out(adder_1_bit_9_carry_out), .\output (\output [4]));
  adder_1_bit adder_1_bit_10 (
    .input_1(input_1[2]), .input_2(input_2[2]), .carry_in(adder_1_bit_12_carry_out),
    .carry_out(adder_1_bit_10_carry_out), .\output (\output [2]));
  adder_1_bit adder_1_bit_11 (
    .input_1(input_1[3]), .input_2(input_2[3]), .carry_in(adder_1_bit_10_carry_out),
    .carry_out(adder_1_bit_11_carry_out), .\output (\output [3]));
  adder_1_bit adder_1_bit_12 (
    .input_1(input_1[1]), .input_2(input_2[1]), .carry_in(adder_1_bit_wo_carry_1_carry_out),
    .carry_out(adder_1_bit_12_carry_out), .\output (\output [1]));
  adder_1_bit_wo_carry adder_1_bit_wo_carry_1 (
    .input_1(input_1[0]), .input_2(input_2[0]), .carry_out(adder_1_bit_wo_carry_1_carry_out),
    .\output (\output [0]));
endmodule

module adder_13_bits_w_clock (
  input  [12:0] input_1,
  input  clock,
  input  [12:0] input_2,
  output c_out,
  output [12:0] \output 
);

  wire adder_1_bit_1_carry_out, adder_1_bit_1_output, adder_1_bit_2_carry_out, adder_1_bit_2_output,
       adder_1_bit_3_carry_out, adder_1_bit_3_output, adder_1_bit_4_carry_out, adder_1_bit_4_output,
       adder_1_bit_5_carry_out, adder_1_bit_5_output, adder_1_bit_6_carry_out, adder_1_bit_6_output,
       adder_1_bit_7_carry_out, adder_1_bit_7_output, adder_1_bit_8_carry_out, adder_1_bit_8_output,
       adder_1_bit_9_carry_out, adder_1_bit_9_output, adder_1_bit_10_carry_out, adder_1_bit_10_output,
       adder_1_bit_11_carry_out, adder_1_bit_11_output, adder_1_bit_12_carry_out, adder_1_bit_12_output,
       adder_1_bit_wo_carry_1_carry_out, adder_1_bit_wo_carry_1_output;

  and and_1 (\output [0], adder_1_bit_wo_carry_1_output, clock);
  and and_2 (\output [1], adder_1_bit_12_output, clock);
  and and_3 (\output [2], adder_1_bit_11_output, clock);
  and and_4 (\output [3], adder_1_bit_10_output, clock);
  and and_5 (\output [4], adder_1_bit_8_output, clock);
  and and_6 (\output [5], adder_1_bit_9_output, clock);
  and and_7 (\output [6], adder_1_bit_7_output, clock);
  and and_8 (\output [7], adder_1_bit_6_output, clock);
  and and_9 (\output [8], adder_1_bit_5_output, clock);
  and and_10 (\output [9], adder_1_bit_4_output, clock);
  and and_11 (\output [10], adder_1_bit_2_output, clock);
  and and_12 (\output [11], adder_1_bit_3_output, clock);
  and and_13 (\output [12], adder_1_bit_1_output, clock);
  and and_14 (c_out, clock, adder_1_bit_1_carry_out);
  adder_1_bit adder_1_bit_1 (
    .input_1(input_1[12]), .input_2(input_2[12]), .carry_in(adder_1_bit_3_carry_out),
    .carry_out(adder_1_bit_1_carry_out), .\output (adder_1_bit_1_output));
  adder_1_bit adder_1_bit_2 (
    .input_1(input_1[10]), .input_2(input_2[10]), .carry_in(adder_1_bit_4_carry_out),
    .carry_out(adder_1_bit_2_carry_out), .\output (adder_1_bit_2_output));
  adder_1_bit adder_1_bit_3 (
    .input_1(input_1[11]), .input_2(input_2[11]), .carry_in(adder_1_bit_2_carry_out),
    .carry_out(adder_1_bit_3_carry_out), .\output (adder_1_bit_3_output));
  adder_1_bit adder_1_bit_4 (
    .input_1(input_1[9]), .input_2(input_2[9]), .carry_in(adder_1_bit_5_carry_out),
    .carry_out(adder_1_bit_4_carry_out), .\output (adder_1_bit_4_output));
  adder_1_bit adder_1_bit_5 (
    .input_1(input_1[8]), .input_2(input_2[8]), .carry_in(adder_1_bit_6_carry_out),
    .carry_out(adder_1_bit_5_carry_out), .\output (adder_1_bit_5_output));
  adder_1_bit adder_1_bit_6 (
    .input_1(input_1[7]), .input_2(input_2[7]), .carry_in(adder_1_bit_7_carry_out),
    .carry_out(adder_1_bit_6_carry_out), .\output (adder_1_bit_6_output));
  adder_1_bit adder_1_bit_7 (
    .input_1(input_1[6]), .input_2(input_2[6]), .carry_in(adder_1_bit_9_carry_out),
    .carry_out(adder_1_bit_7_carry_out), .\output (adder_1_bit_7_output));
  adder_1_bit adder_1_bit_8 (
    .input_1(input_1[4]), .input_2(input_2[4]), .carry_in(adder_1_bit_10_carry_out),
    .carry_out(adder_1_bit_8_carry_out), .\output (adder_1_bit_8_output));
  adder_1_bit adder_1_bit_9 (
    .input_1(input_1[5]), .input_2(input_2[5]), .carry_in(adder_1_bit_8_carry_out),
    .carry_out(adder_1_bit_9_carry_out), .\output (adder_1_bit_9_output));
  adder_1_bit adder_1_bit_10 (
    .input_1(input_1[3]), .input_2(input_2[3]), .carry_in(adder_1_bit_11_carry_out),
    .carry_out(adder_1_bit_10_carry_out), .\output (adder_1_bit_10_output));
  adder_1_bit adder_1_bit_11 (
    .input_1(input_1[2]), .input_2(input_2[2]), .carry_in(adder_1_bit_12_carry_out),
    .carry_out(adder_1_bit_11_carry_out), .\output (adder_1_bit_11_output));
  adder_1_bit adder_1_bit_12 (
    .input_1(input_1[1]), .input_2(input_2[1]), .carry_in(adder_1_bit_wo_carry_1_carry_out),
    .carry_out(adder_1_bit_12_carry_out), .\output (adder_1_bit_12_output));
  adder_1_bit_wo_carry adder_1_bit_wo_carry_1 (
    .input_1(input_1[0]), .input_2(input_2[0]), .carry_out(adder_1_bit_wo_carry_1_carry_out),
    .\output (adder_1_bit_wo_carry_1_output));
endmodule

module adder_18_bits (
  input  [17:0] input_1,
  input  [17:0] input_2,
  output [17:0] \output ,
  output c_out
);

  wire adder_1_bit_2_carry_out, adder_1_bit_3_carry_out, adder_1_bit_4_carry_out, adder_1_bit_5_carry_out,
       adder_1_bit_6_carry_out, adder_1_bit_7_carry_out, adder_1_bit_8_carry_out, adder_1_bit_9_carry_out,
       adder_1_bit_10_carry_out, adder_1_bit_11_carry_out, adder_1_bit_12_carry_out,
       adder_1_bit_13_carry_out, adder_1_bit_14_carry_out, adder_1_bit_15_carry_out,
       adder_1_bit_16_carry_out, adder_1_bit_17_carry_out, adder_1_bit_wo_carry_1_carry_out;

  adder_1_bit adder_1_bit_1 (
    .input_1(input_1[17]), .input_2(input_2[17]), .carry_in(adder_1_bit_3_carry_out), .carry_out(c_out),
    .\output (\output [17]));
  adder_1_bit adder_1_bit_2 (
    .input_1(input_1[15]), .input_2(input_2[15]), .carry_in(adder_1_bit_4_carry_out),
    .carry_out(adder_1_bit_2_carry_out), .\output (\output [15]));
  adder_1_bit adder_1_bit_3 (
    .input_1(input_1[16]), .input_2(input_2[16]), .carry_in(adder_1_bit_2_carry_out),
    .carry_out(adder_1_bit_3_carry_out), .\output (\output [16]));
  adder_1_bit adder_1_bit_4 (
    .input_1(input_1[14]), .input_2(input_2[14]), .carry_in(adder_1_bit_6_carry_out),
    .carry_out(adder_1_bit_4_carry_out), .\output (\output [14]));
  adder_1_bit adder_1_bit_5 (
    .input_1(input_1[12]), .input_2(input_2[12]), .carry_in(adder_1_bit_8_carry_out),
    .carry_out(adder_1_bit_5_carry_out), .\output (\output [12]));
  adder_1_bit adder_1_bit_6 (
    .input_1(input_1[13]), .input_2(input_2[13]), .carry_in(adder_1_bit_5_carry_out),
    .carry_out(adder_1_bit_6_carry_out), .\output (\output [13]));
  adder_1_bit adder_1_bit_7 (
    .input_1(input_1[10]), .input_2(input_2[10]), .carry_in(adder_1_bit_9_carry_out),
    .carry_out(adder_1_bit_7_carry_out), .\output (\output [10]));
  adder_1_bit adder_1_bit_8 (
    .input_1(input_1[11]), .input_2(input_2[11]), .carry_in(adder_1_bit_7_carry_out),
    .carry_out(adder_1_bit_8_carry_out), .\output (\output [11]));
  adder_1_bit adder_1_bit_9 (
    .input_1(input_1[9]), .input_2(input_2[9]), .carry_in(adder_1_bit_10_carry_out),
    .carry_out(adder_1_bit_9_carry_out), .\output (\output [9]));
  adder_1_bit adder_1_bit_10 (
    .input_1(input_1[8]), .input_2(input_2[8]), .carry_in(adder_1_bit_11_carry_out),
    .carry_out(adder_1_bit_10_carry_out), .\output (\output [8]));
  adder_1_bit adder_1_bit_11 (
    .input_1(input_1[7]), .input_2(input_2[7]), .carry_in(adder_1_bit_12_carry_out),
    .carry_out(adder_1_bit_11_carry_out), .\output (\output [7]));
  adder_1_bit adder_1_bit_12 (
    .input_1(input_1[6]), .input_2(input_2[6]), .carry_in(adder_1_bit_13_carry_out),
    .carry_out(adder_1_bit_12_carry_out), .\output (\output [6]));
  adder_1_bit adder_1_bit_13 (
    .input_1(input_1[5]), .input_2(input_2[5]), .carry_in(adder_1_bit_14_carry_out),
    .carry_out(adder_1_bit_13_carry_out), .\output (\output [5]));
  adder_1_bit adder_1_bit_14 (
    .input_1(input_1[4]), .input_2(input_2[4]), .carry_in(adder_1_bit_15_carry_out),
    .carry_out(adder_1_bit_14_carry_out), .\output (\output [4]));
  adder_1_bit adder_1_bit_15 (
    .input_1(input_1[3]), .input_2(input_2[3]), .carry_in(adder_1_bit_16_carry_out),
    .carry_out(adder_1_bit_15_carry_out), .\output (\output [3]));
  adder_1_bit adder_1_bit_16 (
    .input_1(input_1[2]), .input_2(input_2[2]), .carry_in(adder_1_bit_17_carry_out),
    .carry_out(adder_1_bit_16_carry_out), .\output (\output [2]));
  adder_1_bit adder_1_bit_17 (
    .input_1(input_1[1]), .input_2(input_2[1]), .carry_in(adder_1_bit_wo_carry_1_carry_out),
    .carry_out(adder_1_bit_17_carry_out), .\output (\output [1]));
  adder_1_bit_wo_carry adder_1_bit_wo_carry_1 (
    .input_1(input_1[0]), .input_2(input_2[0]), .carry_out(adder_1_bit_wo_carry_1_carry_out),
    .\output (\output [0]));
endmodule

module adder_18_bits_w_clock (
  input  [17:0] input_1,
  input  clock,
  input  [17:0] input_2,
  output c_out,
  output [17:0] \output 
);

  wire adder_1_bit_1_carry_out, adder_1_bit_1_output, adder_1_bit_2_carry_out, adder_1_bit_2_output,
       adder_1_bit_3_carry_out, adder_1_bit_3_output, adder_1_bit_4_carry_out, adder_1_bit_4_output,
       adder_1_bit_5_carry_out, adder_1_bit_5_output, adder_1_bit_6_carry_out, adder_1_bit_6_output,
       adder_1_bit_7_carry_out, adder_1_bit_7_output, adder_1_bit_8_carry_out, adder_1_bit_8_output,
       adder_1_bit_9_carry_out, adder_1_bit_9_output, adder_1_bit_10_carry_out, adder_1_bit_10_output,
       adder_1_bit_11_carry_out, adder_1_bit_11_output, adder_1_bit_12_carry_out, adder_1_bit_12_output,
       adder_1_bit_13_carry_out, adder_1_bit_13_output, adder_1_bit_14_carry_out, adder_1_bit_14_output,
       adder_1_bit_15_carry_out, adder_1_bit_15_output, adder_1_bit_16_carry_out, adder_1_bit_16_output,
       adder_1_bit_17_carry_out, adder_1_bit_17_output, adder_1_bit_wo_carry_1_carry_out,
       adder_1_bit_wo_carry_1_output;

  and and_1 (\output [0], adder_1_bit_wo_carry_1_output, clock);
  and and_2 (\output [1], adder_1_bit_17_output, clock);
  and and_3 (\output [2], adder_1_bit_16_output, clock);
  and and_4 (\output [3], adder_1_bit_15_output, clock);
  and and_5 (\output [4], adder_1_bit_14_output, clock);
  and and_6 (\output [5], adder_1_bit_13_output, clock);
  and and_7 (\output [6], adder_1_bit_12_output, clock);
  and and_8 (\output [7], adder_1_bit_11_output, clock);
  and and_9 (\output [8], adder_1_bit_10_output, clock);
  and and_10 (\output [9], adder_1_bit_9_output, clock);
  and and_11 (\output [10], adder_1_bit_7_output, clock);
  and and_12 (\output [11], adder_1_bit_8_output, clock);
  and and_13 (\output [12], adder_1_bit_6_output, clock);
  and and_14 (\output [13], adder_1_bit_5_output, clock);
  and and_15 (\output [14], adder_1_bit_4_output, clock);
  and and_16 (\output [15], adder_1_bit_3_output, clock);
  and and_17 (\output [16], adder_1_bit_2_output, clock);
  and and_18 (\output [17], adder_1_bit_1_output, clock);
  and and_19 (c_out, clock, adder_1_bit_1_carry_out);
  adder_1_bit adder_1_bit_1 (
    .input_1(input_1[17]), .input_2(input_2[17]), .carry_in(adder_1_bit_2_carry_out),
    .carry_out(adder_1_bit_1_carry_out), .\output (adder_1_bit_1_output));
  adder_1_bit adder_1_bit_2 (
    .input_1(input_1[16]), .input_2(input_2[16]), .carry_in(adder_1_bit_3_carry_out),
    .carry_out(adder_1_bit_2_carry_out), .\output (adder_1_bit_2_output));
  adder_1_bit adder_1_bit_3 (
    .input_1(input_1[15]), .input_2(input_2[15]), .carry_in(adder_1_bit_4_carry_out),
    .carry_out(adder_1_bit_3_carry_out), .\output (adder_1_bit_3_output));
  adder_1_bit adder_1_bit_4 (
    .input_1(input_1[14]), .input_2(input_2[14]), .carry_in(adder_1_bit_5_carry_out),
    .carry_out(adder_1_bit_4_carry_out), .\output (adder_1_bit_4_output));
  adder_1_bit adder_1_bit_5 (
    .input_1(input_1[13]), .input_2(input_2[13]), .carry_in(adder_1_bit_6_carry_out),
    .carry_out(adder_1_bit_5_carry_out), .\output (adder_1_bit_5_output));
  adder_1_bit adder_1_bit_6 (
    .input_1(input_1[12]), .input_2(input_2[12]), .carry_in(adder_1_bit_8_carry_out),
    .carry_out(adder_1_bit_6_carry_out), .\output (adder_1_bit_6_output));
  adder_1_bit adder_1_bit_7 (
    .input_1(input_1[10]), .input_2(input_2[10]), .carry_in(adder_1_bit_9_carry_out),
    .carry_out(adder_1_bit_7_carry_out), .\output (adder_1_bit_7_output));
  adder_1_bit adder_1_bit_8 (
    .input_1(input_1[11]), .input_2(input_2[11]), .carry_in(adder_1_bit_7_carry_out),
    .carry_out(adder_1_bit_8_carry_out), .\output (adder_1_bit_8_output));
  adder_1_bit adder_1_bit_9 (
    .input_1(input_1[9]), .input_2(input_2[9]), .carry_in(adder_1_bit_10_carry_out),
    .carry_out(adder_1_bit_9_carry_out), .\output (adder_1_bit_9_output));
  adder_1_bit adder_1_bit_10 (
    .input_1(input_1[8]), .input_2(input_2[8]), .carry_in(adder_1_bit_11_carry_out),
    .carry_out(adder_1_bit_10_carry_out), .\output (adder_1_bit_10_output));
  adder_1_bit adder_1_bit_11 (
    .input_1(input_1[7]), .input_2(input_2[7]), .carry_in(adder_1_bit_12_carry_out),
    .carry_out(adder_1_bit_11_carry_out), .\output (adder_1_bit_11_output));
  adder_1_bit adder_1_bit_12 (
    .input_1(input_1[6]), .input_2(input_2[6]), .carry_in(adder_1_bit_13_carry_out),
    .carry_out(adder_1_bit_12_carry_out), .\output (adder_1_bit_12_output));
  adder_1_bit adder_1_bit_13 (
    .input_1(input_1[5]), .input_2(input_2[5]), .carry_in(adder_1_bit_14_carry_out),
    .carry_out(adder_1_bit_13_carry_out), .\output (adder_1_bit_13_output));
  adder_1_bit adder_1_bit_14 (
    .input_1(input_1[4]), .input_2(input_2[4]), .carry_in(adder_1_bit_15_carry_out),
    .carry_out(adder_1_bit_14_carry_out), .\output (adder_1_bit_14_output));
  adder_1_bit adder_1_bit_15 (
    .input_1(input_1[3]), .input_2(input_2[3]), .carry_in(adder_1_bit_16_carry_out),
    .carry_out(adder_1_bit_15_carry_out), .\output (adder_1_bit_15_output));
  adder_1_bit adder_1_bit_16 (
    .input_1(input_1[2]), .input_2(input_2[2]), .carry_in(adder_1_bit_17_carry_out),
    .carry_out(adder_1_bit_16_carry_out), .\output (adder_1_bit_16_output));
  adder_1_bit adder_1_bit_17 (
    .input_1(input_1[1]), .input_2(input_2[1]), .carry_in(adder_1_bit_wo_carry_1_carry_out),
    .carry_out(adder_1_bit_17_carry_out), .\output (adder_1_bit_17_output));
  adder_1_bit_wo_carry adder_1_bit_wo_carry_1 (
    .input_1(input_1[0]), .input_2(input_2[0]), .carry_out(adder_1_bit_wo_carry_1_carry_out),
    .\output (adder_1_bit_wo_carry_1_output));
endmodule

module zero_ext_6_bits (
  input  [5:0] in_1,
  output [17:0] out_2
);


  assign out_2 = {{12{1'b0}}, in_1};
endmodule

module zero_ext_9_bits (
  input  [8:0] in_1,
  output [17:0] out_2
);


  assign out_2 = {{9{1'b0}}, in_1};
endmodule

module zero_ext_10_bits (
  input  [9:0] in_1,
  output [17:0] out_2
);


  assign out_2 = {{8{1'b0}}, in_1};
endmodule

module zero_ext_12_bits (
  input  [11:0] in_1,
  output [17:0] out_2
);


  assign out_2 = {{6{1'b0}}, in_1};
endmodule

module zero_ext_13_bits (
  input  [12:0] in_1,
  output [17:0] out_2
);


  assign out_2 = {{5{1'b0}}, in_1};
endmodule

module zero_extent_10to12 (
  input  [9:0] in_1,
  output [11:0] out_2
);


  assign out_2 = {2'b00, in_1};
endmodule

module _12_to_13_zero_ext (
  input  [11:0] in_1,
  output [12:0] out_2
);


  assign out_2 = {1'b0, in_1};
endmodule

module sign_ext_6_bits (
  input  [5:0] in_1,
  output [17:0] out_2
);

  Multiplexer #(.enable("false")) multiplexer_1 (.in0(1'b0), .in1(1'b1), .out(out_2[17]), .sel(in_1[5]));

  assign out_2[16:0] = {{11{out_2[17]}}, in_1};
endmodule

module sign_ext_9_bits (
  input  [8:0] in_1,
  output [17:0] out_2
);

  Multiplexer #(.enable("false")) multiplexer_1 (.in0(1'b0), .in1(1'b1), .out(out_2[17]), .sel(in_1[8]));

  assign out_2[16:0] = {{8{out_2[17]}}, in_1};
endmodule

module sign_ext_10_bits (
  input  [9:0] in_1,
  output [17:0] out_2
);

  Multiplexer #(.enable("false")) multiplexer_1 (.in0(1'b0), .in1(1'b1), .out(out_2[17]), .sel(in_1[9]));

  assign out_2[16:0] = {{7{out_2[17]}}, in_1};
endmodule

module sign_ext_12_bits (
  input  [11:0] in_1,
  output [17:0] out_2
);

  Multiplexer #(.enable("false")) multiplexer_1 (.in0(1'b0), .in1(1'b1), .out(out_2[17]), .sel(in_1[11]));

  assign out_2[16:0] = {{5{out_2[17]}}, in_1};
endmodule

module sign_ext_13_bits (
  input  [12:0] in_1,
  output [17:0] out_2
);

  Multiplexer #(.enable("false")) multiplexer_1 (.in0(1'b0), .in1(1'b1), .out(out_2[17]), .sel(in_1[12]));

  assign out_2[16:0] = {{4{out_2[17]}}, in_1};
endmodule

module _13_to_12_converter (
  input  [12:0] in_1,
  output [11:0] out_2
);


  assign out_2 = in_1[11:0];
endmodule

module REGISTER_FILE (
  input  we,
  input  reset,
  input  clock,
  input  [17:0] \input ,
  input  [3:0] ra1,
  input  [3:0] wr,
  input  [3:0] ra2,
  output [17:0] rd1,
  output [17:0] rd2,
  output [17:0] stack_pointer_register
);

  wire and_1_out, and_2_out, and_3_out, and_4_out, and_5_out, and_6_out, and_7_out, and_8_out, and_9_out,
       and_10_out, and_11_out, and_12_out, and_13_out, and_14_out, and_15_out, and_16_out, decoder_1_out0,
       decoder_1_out1, decoder_1_out2, decoder_1_out3, decoder_1_out4, decoder_1_out5, decoder_1_out6,
       decoder_1_out7, decoder_1_out8, decoder_1_out9, decoder_1_out10, decoder_1_out11, decoder_1_out12,
       decoder_1_out13, decoder_1_out14, decoder_1_out15;
  wire [17:0] multiplexer_1_out, multiplexer_2_out, multiplexer_3_out, multiplexer_4_out, multiplexer_5_out,
       multiplexer_6_out, multiplexer_7_out, multiplexer_8_out, multiplexer_9_out, multiplexer_10_out,
       multiplexer_11_out, multiplexer_12_out, multiplexer_13_out, multiplexer_14_out, multiplexer_15_out,
       multiplexer_16_out, multiplexer_17_out, multiplexer_18_out, multiplexer_19_out, multiplexer_20_out,
       multiplexer_21_out, multiplexer_22_out, multiplexer_23_out, multiplexer_24_out, multiplexer_25_out,
       multiplexer_26_out, multiplexer_27_out, multiplexer_28_out, multiplexer_29_out, multiplexer_30_out,
       multiplexer_31_out, multiplexer_32_out, register_18_bit_1_out_3, register_18_bit_2_out_3,
       register_18_bit_3_out_3, register_18_bit_4_out_3, register_18_bit_5_out_3, register_18_bit_6_out_3,
       register_18_bit_7_out_3, register_18_bit_8_out_3, register_18_bit_9_out_3, register_18_bit_10_out_3,
       register_18_bit_11_out_3, register_18_bit_12_out_3, register_18_bit_13_out_3,
       register_18_bit_14_out_3, register_18_bit_16_out_3;

  Decoder #(.select(4), .enable("false")) decoder_1 (
    .out0(decoder_1_out0), .out1(decoder_1_out1), .out2(decoder_1_out2), .out3(decoder_1_out3),
    .out4(decoder_1_out4), .out5(decoder_1_out5), .out6(decoder_1_out6), .out7(decoder_1_out7),
    .out8(decoder_1_out8), .out9(decoder_1_out9), .out10(decoder_1_out10), .out11(decoder_1_out11),
    .out12(decoder_1_out12), .out13(decoder_1_out13), .out14(decoder_1_out14), .out15(decoder_1_out15),
    .sel(wr));
  and and_1 (and_1_out, decoder_1_out0, we);
  and and_2 (and_2_out, decoder_1_out1, we);
  and and_3 (and_3_out, decoder_1_out2, we);
  and and_4 (and_4_out, decoder_1_out3, we);
  and and_5 (and_5_out, decoder_1_out4, we);
  and and_6 (and_6_out, decoder_1_out5, we);
  and and_7 (and_7_out, decoder_1_out6, we);
  and and_8 (and_8_out, decoder_1_out7, we);
  and and_9 (and_9_out, decoder_1_out8, we);
  and and_10 (and_10_out, decoder_1_out9, we);
  and and_11 (and_11_out, decoder_1_out10, we);
  and and_12 (and_12_out, decoder_1_out11, we);
  and and_13 (and_13_out, decoder_1_out12, we);
  and and_14 (and_14_out, decoder_1_out13, we);
  and and_15 (and_15_out, decoder_1_out14, we);
  and and_16 (and_16_out, decoder_1_out15, we);
  Multiplexer #(.width(18), .enable("false")) multiplexer_1 (
    .in0(register_18_bit_1_out_3), .in1(\input ), .out(multiplexer_1_out), .sel(and_1_out));
  Multiplexer #(.width(18), .enable("false")) multiplexer_2 (
    .in0(multiplexer_1_out), .in1({18{1'b0}}), .out(multiplexer_2_out), .sel(reset));
  Multiplexer #(.width(18), .enable("false")) multiplexer_3 (
    .in0(register_18_bit_2_out_3), .in1(\input ), .out(multiplexer_3_out), .sel(and_2_out));
  Multiplexer #(.width(18), .enable("false")) multiplexer_4 (
    .in0(multiplexer_3_out), .in1({18{1'b0}}), .out(multiplexer_4_out), .sel(reset));
  Multiplexer #(.width(18), .enable("false")) multiplexer_5 (
    .in0(register_18_bit_3_out_3), .in1(\input ), .out(multiplexer_5_out), .sel(and_3_out));
  Multiplexer #(.width(18), .enable("false")) multiplexer_6 (
    .in0(multiplexer_5_out), .in1({18{1'b0}}), .out(multiplexer_6_out), .sel(reset));
  Multiplexer #(.width(18), .enable("false")) multiplexer_7 (
    .in0(register_18_bit_4_out_3), .in1(\input ), .out(multiplexer_7_out), .sel(and_4_out));
  Multiplexer #(.width(18), .enable("false")) multiplexer_8 (
    .in0(multiplexer_7_out), .in1({18{1'b0}}), .out(multiplexer_8_out), .sel(reset));
  Multiplexer #(.width(18), .enable("false")) multiplexer_9 (
    .in0(register_18_bit_5_out_3), .in1(\input ), .out(multiplexer_9_out), .sel(and_5_out));
  Multiplexer #(.width(18), .enable("false")) multiplexer_10 (
    .in0(multiplexer_9_out), .in1({18{1'b0}}), .out(multiplexer_10_out), .sel(reset));
  Multiplexer #(.width(18), .enable("false")) multiplexer_11 (
    .in0(register_18_bit_6_out_3), .in1(\input ), .out(multiplexer_11_out), .sel(and_6_out));
  Multiplexer #(.width(18), .enable("false")) multiplexer_12 (
    .in0(multiplexer_11_out), .in1({18{1'b0}}), .out(multiplexer_12_out), .sel(reset));
  Multiplexer #(.width(18), .enable("false")) multiplexer_13 (
    .in0(register_18_bit_7_out_3), .in1(\input ), .out(multiplexer_13_out), .sel(and_7_out));
  Multiplexer #(.width(18), .enable("false")) multiplexer_14 (
    .in0(multiplexer_13_out), .in1({18{1'b0}}), .out(multiplexer_14_out), .sel(reset));
  Multiplexer #(.width(18), .enable("false")) multiplexer_15 (
    .in0(register_18_bit_8_out_3), .in1(\input ), .out(multiplexer_15_out), .sel(and_8_out));
  Multiplexer #(.width(18), .enable("false")) multiplexer_16 (
    .in0(multiplexer_15_out), .in1({18{1'b0}}), .out(multiplexer_16_out), .sel(reset));
  Multiplexer #(.width(18), .enable("false")) multiplexer_17 (
    .in0(register_18_bit_9_out_3), .in1(\input ), .out(multiplexer_17_out), .sel(and_9_out));
  Multiplexer #(.width(18), .enable("false")) multiplexer_18 (
    .in0(multiplexer_17_out), .in1({18{1'b0}}), .out(multiplexer_18_out), .sel(reset));
  Multiplexer #(.width(18), .enable("false")) multiplexer_19 (
    .in0(register_18_bit_10_out_3), .in1(\input ), .out(multiplexer_19_out), .sel(and_10_out));
  Multiplexer #(.width(18), .enable("false")) multiplexer_20 (
    .in0(multiplexer_19_out), .in1({18{1'b0}}), .out(multiplexer_20_out), .sel(reset));
  Multiplexer #(.width(18), .enable("false")) multiplexer_21 (
    .in0(register_18_bit_11_out_3), .in1(\input ), .out(multiplexer_21_out), .sel(and_11_out));
  Multiplexer #(.width(18), .enable("false")) multiplexer_22 (
    .in0(multiplexer_21_out), .in1({18{1'b0}}), .out(multiplexer_22_out), .sel(reset));
  Multiplexer #(.width(18), .enable("false")) multiplexer_23 (
    .in0(register_18_bit_12_out_3), .in1(\input ), .out(multiplexer_23_out), .sel(and_12_out));
  Multiplexer #(.width(18), .enable("false")) multiplexer_24 (
    .in0(multiplexer_23_out), .in1({18{1'b0}}), .out(multiplexer_24_out), .sel(reset));
  Multiplexer #(.width(18), .enable("false")) multiplexer_25 (
    .in0(register_18_bit_13_out_3), .in1(\input ), .out(multiplexer_25_out), .sel(and_13_out));
  Multiplexer #(.width(18), .enable("false")) multiplexer_26 (
    .in0(multiplexer_25_out), .in1({18{1'b0}}), .out(multiplexer_26_out), .sel(reset));
  Multiplexer #(.width(18), .enable("false")) multiplexer_27 (
    .in0(register_18_bit_14_out_3), .in1(\input ), .out(multiplexer_27_out), .sel(and_14_out));
  Multiplexer #(.width(18), .enable("false")) multiplexer_28 (
    .in0(multiplexer_27_out), .in1({18{1'b0}}), .out(multiplexer_28_out), .sel(reset));
  Multiplexer #(.width(18), .enable("false")) multiplexer_29 (
    .in0(stack_pointer_register), .in1(\input ), .out(multiplexer_29_out), .sel(and_15_out));
  Multiplexer #(.width(18), .enable("false")) multiplexer_30 (
    .in0(multiplexer_29_out), .in1({18{1'b0}}), .out(multiplexer_30_out), .sel(reset));
  Multiplexer #(.width(18), .enable("false")) multiplexer_31 (
    .in0(register_18_bit_16_out_3), .in1(\input ), .out(multiplexer_31_out), .sel(and_16_out));
  Multiplexer #(.width(18), .enable("false")) multiplexer_32 (
    .in0(multiplexer_31_out), .in1({18{1'b0}}), .out(multiplexer_32_out), .sel(reset));
  register_18_bit register_18_bit_1 (.in_1(multiplexer_2_out), .in_2(clock), .out_3(register_18_bit_1_out_3));
  register_18_bit register_18_bit_2 (.in_1(multiplexer_4_out), .in_2(clock), .out_3(register_18_bit_2_out_3));
  register_18_bit register_18_bit_3 (.in_1(multiplexer_6_out), .in_2(clock), .out_3(register_18_bit_3_out_3));
  register_18_bit register_18_bit_4 (.in_1(multiplexer_8_out), .in_2(clock), .out_3(register_18_bit_4_out_3));
  register_18_bit register_18_bit_5 (.in_1(multiplexer_10_out), .in_2(clock), .out_3(register_18_bit_5_out_3));
  register_18_bit register_18_bit_6 (.in_1(multiplexer_12_out), .in_2(clock), .out_3(register_18_bit_6_out_3));
  register_18_bit register_18_bit_7 (.in_1(multiplexer_14_out), .in_2(clock), .out_3(register_18_bit_7_out_3));
  register_18_bit register_18_bit_8 (.in_1(multiplexer_16_out), .in_2(clock), .out_3(register_18_bit_8_out_3));
  register_18_bit register_18_bit_9 (.in_1(multiplexer_18_out), .in_2(clock), .out_3(register_18_bit_9_out_3));
  register_18_bit register_18_bit_10 (.in_1(multiplexer_20_out), .in_2(clock), .out_3(register_18_bit_10_out_3));
  register_18_bit register_18_bit_11 (.in_1(multiplexer_22_out), .in_2(clock), .out_3(register_18_bit_11_out_3));
  register_18_bit register_18_bit_12 (.in_1(multiplexer_24_out), .in_2(clock), .out_3(register_18_bit_12_out_3));
  register_18_bit register_18_bit_13 (.in_1(multiplexer_26_out), .in_2(clock), .out_3(register_18_bit_13_out_3));
  register_18_bit register_18_bit_14 (.in_1(multiplexer_28_out), .in_2(clock), .out_3(register_18_bit_14_out_3));
  register_18_bit register_18_bit_15 (.in_1(multiplexer_30_out), .in_2(clock), .out_3(stack_pointer_register));
  register_18_bit register_18_bit_16 (.in_1(multiplexer_32_out), .in_2(clock), .out_3(register_18_bit_16_out_3));
  Multiplexer #(.select(4), .width(18), .enable("false")) multiplexer_33 (
    .in0(register_18_bit_1_out_3), .in1(register_18_bit_2_out_3), .in2(register_18_bit_3_out_3),
    .in3(register_18_bit_4_out_3), .in4(register_18_bit_5_out_3), .in5(register_18_bit_6_out_3),
    .in6(register_18_bit_7_out_3), .in7(register_18_bit_8_out_3), .in8(register_18_bit_9_out_3),
    .in9(register_18_bit_10_out_3), .in10(register_18_bit_11_out_3), .in11(register_18_bit_12_out_3),
    .in12(register_18_bit_13_out_3), .in13(register_18_bit_14_out_3), .in14(stack_pointer_register),
    .in15(register_18_bit_16_out_3), .out(rd1), .sel(ra1));
  Multiplexer #(.select(4), .width(18), .enable("false")) multiplexer_34 (
    .in0(register_18_bit_1_out_3), .in1(register_18_bit_2_out_3), .in2(register_18_bit_3_out_3),
    .in3(register_18_bit_4_out_3), .in4(register_18_bit_5_out_3), .in5(register_18_bit_6_out_3),
    .in6(register_18_bit_7_out_3), .in7(register_18_bit_8_out_3), .in8(register_18_bit_9_out_3),
    .in9(register_18_bit_10_out_3), .in10(register_18_bit_11_out_3), .in11(register_18_bit_12_out_3),
    .in12(register_18_bit_13_out_3), .in13(register_18_bit_14_out_3), .in14(stack_pointer_register),
    .in15(register_18_bit_16_out_3), .out(rd2), .sel(ra2));
endmodule

module converter_10__9__18_upper (
  input  [9:0] in,
  output [17:0] out
);


  assign out = {in[8:0], {9{1'b0}}};
endmodule

module _18b_to_12b_converter (
  input  [17:0] \input ,
  output [11:0] \output 
);


  assign \output  = \input [11:0];
endmodule
